// Logisim project Decoder.circ as structural Verilog
module decoder (
  input  A0,
  input  A1,
  output O0,
  output O1,
  output O2,
  output O3
);

  wire not_1_out, not_2_out, not_3_out, not_4_out;

  not not_1 (not_1_out, A0);
  not not_2 (not_2_out, A1);
  not not_3 (not_3_out, A0);
  not not_4 (not_4_out, A1);
  and and_1 (O3, A0, A1);
  and and_2 (O0, not_1_out, not_2_out);
  and and_3 (O1, not_3_out, A1);
  and and_4 (O2, A0, not_4_out);
endmodule
