// Logisim project PBL_MIps_32Bit_Single_Cycle_Processor.circ as structural Verilog: 2 circuits, main circuit SINGLE_CYCLE
module SINGLE_CYCLE (
);

  RAM #(.addrWidth(16), .dataWidth(32), .bus("separate")) ram_1 ();  // open: addr, din, data, str, sel, clk, ld, clr
  // control_unit Control_Unit: pin names not known
  _5BIT_REGISTER_FILE u_5bit_register_file_1 ();  // open: A1, A2, WD, A3, Write_EN, RD1, RD2, CLK
  // ALUControl ALUControl: pin names not known
  // ALU ALU: pin names not known
  RAM #(.addrWidth(16), .dataWidth(32), .bus("separate")) ram_2 ();  // open: addr, din, data, str, sel, clk, ld, clr

  // Notes on the sheet:
  //   Instruction Memory
  //   Data Memory
endmodule

module _5BIT_REGISTER_FILE (
  input  [4:0] A1,
  input  CLK,
  input  [4:0] A2,
  input  [31:0] WD,
  input  [4:0] A3,
  input  Write_EN,
  output [31:0] RD1,
  output [31:0] RD2
);

  wire demultiplexer_2_out0, demultiplexer_2_out1, demultiplexer_2_out2, demultiplexer_2_out3,
       demultiplexer_2_out4, demultiplexer_2_out5, demultiplexer_2_out6, demultiplexer_2_out7,
       demultiplexer_2_out8, demultiplexer_2_out9, demultiplexer_2_out10, demultiplexer_2_out11,
       demultiplexer_2_out12, demultiplexer_2_out13, demultiplexer_2_out14, demultiplexer_2_out15,
       demultiplexer_2_out16, demultiplexer_2_out17, demultiplexer_2_out18, demultiplexer_2_out19,
       demultiplexer_2_out20, demultiplexer_2_out21, demultiplexer_2_out22, demultiplexer_2_out23,
       demultiplexer_2_out24, demultiplexer_2_out25, demultiplexer_2_out26, demultiplexer_2_out27,
       demultiplexer_2_out28, demultiplexer_2_out29, demultiplexer_2_out30, demultiplexer_2_out31;
  wire [31:0] Address_00000_q, Address_00001_q, Address_00010_q, Address_00011_q, Address_00100_q,
       Address_00101_q, Address_00110_q, Address_00111_q, Address_01000_q, Address_01001_q, Address_01010_q,
       Address_01011_q, Address_01100_q, Address_01101_q, Address_01110_q, Address_01111_q, Address_10000_q,
       Address_10001_q, Address_10010_q, Address_10011_q, Address_10100_q, Address_10101_q, Address_10110_q,
       Address_10111_q, Address_11000_q, Address_11001_q, Address_11010_q, Address_11011_q, Address_11100_q,
       Address_11101_q, Address_11110_q, Address_11111_q, demultiplexer_1_out0, demultiplexer_1_out1,
       demultiplexer_1_out2, demultiplexer_1_out3, demultiplexer_1_out4, demultiplexer_1_out5,
       demultiplexer_1_out6, demultiplexer_1_out7, demultiplexer_1_out8, demultiplexer_1_out9,
       demultiplexer_1_out10, demultiplexer_1_out11, demultiplexer_1_out12, demultiplexer_1_out13,
       demultiplexer_1_out14, demultiplexer_1_out15, demultiplexer_1_out16, demultiplexer_1_out17,
       demultiplexer_1_out18, demultiplexer_1_out19, demultiplexer_1_out20, demultiplexer_1_out21,
       demultiplexer_1_out22, demultiplexer_1_out23, demultiplexer_1_out24, demultiplexer_1_out25,
       demultiplexer_1_out26, demultiplexer_1_out27, demultiplexer_1_out28, demultiplexer_1_out29,
       demultiplexer_1_out30, demultiplexer_1_out31;

  Demultiplexer #(.select(5), .width(32)) demultiplexer_1 (
    .out0(demultiplexer_1_out0), .out1(demultiplexer_1_out1), .out2(demultiplexer_1_out2),
    .out3(demultiplexer_1_out3), .out4(demultiplexer_1_out4), .out5(demultiplexer_1_out5),
    .out6(demultiplexer_1_out6), .out7(demultiplexer_1_out7), .out8(demultiplexer_1_out8),
    .out9(demultiplexer_1_out9), .out10(demultiplexer_1_out10), .out11(demultiplexer_1_out11),
    .out12(demultiplexer_1_out12), .out13(demultiplexer_1_out13), .out14(demultiplexer_1_out14),
    .out15(demultiplexer_1_out15), .out16(demultiplexer_1_out16), .out17(demultiplexer_1_out17),
    .out18(demultiplexer_1_out18), .out19(demultiplexer_1_out19), .out20(demultiplexer_1_out20),
    .out21(demultiplexer_1_out21), .out22(demultiplexer_1_out22), .out23(demultiplexer_1_out23),
    .out24(demultiplexer_1_out24), .out25(demultiplexer_1_out25), .out26(demultiplexer_1_out26),
    .out27(demultiplexer_1_out27), .out28(demultiplexer_1_out28), .out29(demultiplexer_1_out29),
    .out30(demultiplexer_1_out30), .out31(demultiplexer_1_out31), .in(WD), .sel(A3));  // open: en
  Demultiplexer #(.select(5)) demultiplexer_2 (
    .out0(demultiplexer_2_out0), .out1(demultiplexer_2_out1), .out2(demultiplexer_2_out2),
    .out3(demultiplexer_2_out3), .out4(demultiplexer_2_out4), .out5(demultiplexer_2_out5),
    .out6(demultiplexer_2_out6), .out7(demultiplexer_2_out7), .out8(demultiplexer_2_out8),
    .out9(demultiplexer_2_out9), .out10(demultiplexer_2_out10), .out11(demultiplexer_2_out11),
    .out12(demultiplexer_2_out12), .out13(demultiplexer_2_out13), .out14(demultiplexer_2_out14),
    .out15(demultiplexer_2_out15), .out16(demultiplexer_2_out16), .out17(demultiplexer_2_out17),
    .out18(demultiplexer_2_out18), .out19(demultiplexer_2_out19), .out20(demultiplexer_2_out20),
    .out21(demultiplexer_2_out21), .out22(demultiplexer_2_out22), .out23(demultiplexer_2_out23),
    .out24(demultiplexer_2_out24), .out25(demultiplexer_2_out25), .out26(demultiplexer_2_out26),
    .out27(demultiplexer_2_out27), .out28(demultiplexer_2_out28), .out29(demultiplexer_2_out29),
    .out30(demultiplexer_2_out30), .out31(demultiplexer_2_out31), .in(Write_EN), .sel(A3));  // open: en
  Register #(.width(32)) Address_00000 (
    .D(demultiplexer_1_out0), .en(demultiplexer_2_out0), .Q(Address_00000_q), .clk(CLK));  // open: clr
  Register #(.width(32)) Address_00001 (
    .D(demultiplexer_1_out1), .en(demultiplexer_2_out1), .Q(Address_00001_q), .clk(CLK));  // open: clr
  Register #(.width(32)) Address_00010 (
    .D(demultiplexer_1_out2), .en(demultiplexer_2_out2), .Q(Address_00010_q), .clk(CLK));  // open: clr
  Register #(.width(32)) Address_00011 (
    .D(demultiplexer_1_out3), .en(demultiplexer_2_out3), .Q(Address_00011_q), .clk(CLK));  // open: clr
  Register #(.width(32)) Address_00100 (
    .D(demultiplexer_1_out4), .en(demultiplexer_2_out4), .Q(Address_00100_q), .clk(CLK));  // open: clr
  Register #(.width(32)) Address_00101 (
    .D(demultiplexer_1_out5), .en(demultiplexer_2_out5), .Q(Address_00101_q), .clk(CLK));  // open: clr
  Register #(.width(32)) Address_00110 (
    .D(demultiplexer_1_out6), .en(demultiplexer_2_out6), .Q(Address_00110_q), .clk(CLK));  // open: clr
  Register #(.width(32)) Address_00111 (
    .D(demultiplexer_1_out7), .en(demultiplexer_2_out7), .Q(Address_00111_q), .clk(CLK));  // open: clr
  Register #(.width(32)) Address_01000 (
    .D(demultiplexer_1_out8), .en(demultiplexer_2_out8), .Q(Address_01000_q), .clk(CLK));  // open: clr
  Register #(.width(32)) Address_01001 (
    .D(demultiplexer_1_out9), .en(demultiplexer_2_out9), .Q(Address_01001_q), .clk(CLK));  // open: clr
  Register #(.width(32)) Address_01010 (
    .D(demultiplexer_1_out10), .en(demultiplexer_2_out10), .Q(Address_01010_q), .clk(CLK));  // open: clr
  Register #(.width(32)) Address_01011 (
    .D(demultiplexer_1_out11), .en(demultiplexer_2_out11), .Q(Address_01011_q), .clk(CLK));  // open: clr
  Register #(.width(32)) Address_01100 (
    .D(demultiplexer_1_out12), .en(demultiplexer_2_out12), .Q(Address_01100_q), .clk(CLK));  // open: clr
  Register #(.width(32)) Address_01101 (
    .D(demultiplexer_1_out13), .en(demultiplexer_2_out13), .Q(Address_01101_q), .clk(CLK));  // open: clr
  Register #(.width(32)) Address_01110 (
    .D(demultiplexer_1_out14), .en(demultiplexer_2_out14), .Q(Address_01110_q), .clk(CLK));  // open: clr
  Register #(.width(32)) Address_01111 (
    .D(demultiplexer_1_out15), .en(demultiplexer_2_out15), .Q(Address_01111_q), .clk(CLK));  // open: clr
  Register #(.width(32)) Address_10000 (
    .D(demultiplexer_1_out16), .en(demultiplexer_2_out16), .Q(Address_10000_q), .clk(CLK));  // open: clr
  Register #(.width(32)) Address_10001 (
    .D(demultiplexer_1_out17), .en(demultiplexer_2_out17), .Q(Address_10001_q), .clk(CLK));  // open: clr
  Register #(.width(32)) Address_10010 (
    .D(demultiplexer_1_out18), .en(demultiplexer_2_out18), .Q(Address_10010_q), .clk(CLK));  // open: clr
  Register #(.width(32)) Address_10011 (
    .D(demultiplexer_1_out19), .en(demultiplexer_2_out19), .Q(Address_10011_q), .clk(CLK));  // open: clr
  Register #(.width(32)) Address_10100 (
    .D(demultiplexer_1_out20), .en(demultiplexer_2_out20), .Q(Address_10100_q), .clk(CLK));  // open: clr
  Register #(.width(32)) Address_10101 (
    .D(demultiplexer_1_out21), .en(demultiplexer_2_out21), .Q(Address_10101_q), .clk(CLK));  // open: clr
  Register #(.width(32)) Address_10110 (
    .D(demultiplexer_1_out22), .en(demultiplexer_2_out22), .Q(Address_10110_q), .clk(CLK));  // open: clr
  Register #(.width(32)) Address_10111 (
    .D(demultiplexer_1_out23), .en(demultiplexer_2_out23), .Q(Address_10111_q), .clk(CLK));  // open: clr
  Register #(.width(32)) Address_11000 (
    .D(demultiplexer_1_out24), .en(demultiplexer_2_out24), .Q(Address_11000_q), .clk(CLK));  // open: clr
  Register #(.width(32)) Address_11001 (
    .D(demultiplexer_1_out25), .en(demultiplexer_2_out25), .Q(Address_11001_q), .clk(CLK));  // open: clr
  Register #(.width(32)) Address_11010 (
    .D(demultiplexer_1_out26), .en(demultiplexer_2_out26), .Q(Address_11010_q), .clk(CLK));  // open: clr
  Register #(.width(32)) Address_11011 (
    .D(demultiplexer_1_out27), .en(demultiplexer_2_out27), .Q(Address_11011_q), .clk(CLK));  // open: clr
  Register #(.width(32)) Address_11100 (
    .D(demultiplexer_1_out28), .en(demultiplexer_2_out28), .Q(Address_11100_q), .clk(CLK));  // open: clr
  Register #(.width(32)) Address_11101 (
    .D(demultiplexer_1_out29), .en(demultiplexer_2_out29), .Q(Address_11101_q), .clk(CLK));  // open: clr
  Register #(.width(32)) Address_11110 (
    .D(demultiplexer_1_out30), .en(demultiplexer_2_out30), .Q(Address_11110_q), .clk(CLK));  // open: clr
  Register #(.width(32)) Address_11111 (
    .D(demultiplexer_1_out31), .en(demultiplexer_2_out31), .Q(Address_11111_q), .clk(CLK));  // open: clr
  Multiplexer #(.select(5), .width(32)) multiplexer_1 (
    .in0(Address_00000_q), .in1(Address_00001_q), .in2(Address_00010_q), .in3(Address_00011_q),
    .in4(Address_00100_q), .in5(Address_00101_q), .in6(Address_00110_q), .in7(Address_00111_q),
    .in8(Address_01000_q), .in9(Address_01001_q), .in10(Address_01010_q), .in11(Address_01011_q),
    .in12(Address_01100_q), .in13(Address_01101_q), .in14(Address_01110_q), .in15(Address_01111_q),
    .in16(Address_10000_q), .in17(Address_10001_q), .in18(Address_10010_q), .in19(Address_10011_q),
    .in20(Address_10100_q), .in21(Address_10101_q), .in22(Address_10110_q), .in23(Address_10111_q),
    .in24(Address_11000_q), .in25(Address_11001_q), .in26(Address_11010_q), .in27(Address_11011_q),
    .in28(Address_11100_q), .in29(Address_11101_q), .in30(Address_11110_q), .in31(Address_11111_q),
    .out(RD1), .sel(A1));  // open: en
  Multiplexer #(.select(5), .width(32)) multiplexer_2 (
    .in0(Address_00000_q), .in1(Address_00001_q), .in2(Address_00010_q), .in3(Address_00011_q),
    .in4(Address_00100_q), .in5(Address_00101_q), .in6(Address_00110_q), .in7(Address_00111_q),
    .in8(Address_01000_q), .in9(Address_01001_q), .in10(Address_01010_q), .in11(Address_01011_q),
    .in12(Address_01100_q), .in13(Address_01101_q), .in14(Address_01110_q), .in15(Address_01111_q),
    .in16(Address_10000_q), .in17(Address_10001_q), .in18(Address_10010_q), .in19(Address_10011_q),
    .in20(Address_10100_q), .in21(Address_10101_q), .in22(Address_10110_q), .in23(Address_10111_q),
    .in24(Address_11000_q), .in25(Address_11001_q), .in26(Address_11010_q), .in27(Address_11011_q),
    .in28(Address_11100_q), .in29(Address_11101_q), .in30(Address_11110_q), .in31(Address_11111_q),
    .out(RD2), .sel(A2));  // open: en
endmodule
