// Logisim project Practice 1.circ as structural Verilog: 1 circuit, main circuit main
module main (
  input  [3:0] I0,
  input  [3:0] I1,
  input  [3:0] I2,
  input  [3:0] I3,
  output [3:0] Out0,
  output [3:0] Out1
);

  assign Out0 = I0 & I1;  // AND_Gate and_1, 4 bits wide
  assign Out1 = I2 & I3;  // AND_Gate and_2, 4 bits wide
endmodule
