// Logisim project SingleCycleProcessor.circ as structural Verilog: 17 circuits, main circuit SingleCycleProcessor
module ALU (
  input  [31:0] in_A,
  input  [31:0] in_B,
  input  [5:0] opcode,
  output [31:0] out_C,
  output carryout,
  output zero,
  output overflow
);

  wire add_carry_out, add_overflow, equal_2_result, equal_3_result, equal_4_result, equal_5_result,
       equal_6_result, equal_7_result, equal_8_result, equal_9_result, equal_10_result, equal_result,
       mult_carry_out, mult_overflow, sub_carry_out, sub_overflow;
  wire [31:0] add_result, and_result, mult_result, or_result, sll_result, slt_result, sra_result, srl_result,
       sub_result, xor_result;

  _32_bit_subs sub (.A(in_A), .B(in_B), .carry_out(sub_carry_out), .overflow(sub_overflow), .Result(sub_result));
  _32_bit_adder u_32_bit_adder_1 (
    .A(in_A), .B(in_B), .carry_out(add_carry_out), .overflow(add_overflow), .Result(add_result));
  mult mult_1 (.A(in_A), .B(in_B), .carry_out(mult_carry_out), .overflow(mult_overflow), .Result(mult_result));
  \and  \and  (.A(in_A), .B(in_B), .Result(and_result));
  \or  \or  (.A(in_A), .b(in_B), .Result(or_result));
  \xor  \xor  (.A(in_A), .B(in_B), .Result(xor_result));
  shift_left sll (.A(in_A), .B(in_B), .Result(sll_result));
  set_less_than slt (.A(in_A), .B(in_B), .Result(slt_result));
  shift_arithmetic_right sra (.A(in_A), .B(in_B), .Result(sra_result));
  shift_logical_right srl (.A(in_A), .B(in_B), .Result(srl_result));
  equal equal (.A(sub_result), .B({32{1'b0}}), .Result(equal_result));
  equal equal_2 (.A(add_result), .B({32{1'b0}}), .Result(equal_2_result));
  equal equal_3 (.A(mult_result), .B({32{1'b0}}), .Result(equal_3_result));
  equal equal_4 (.A(and_result), .B({32{1'b0}}), .Result(equal_4_result));
  equal equal_5 (.A(or_result), .B({32{1'b0}}), .Result(equal_5_result));
  equal equal_6 (.A(xor_result), .B({32{1'b0}}), .Result(equal_6_result));
  equal equal_7 (.A(sll_result), .B({32{1'b0}}), .Result(equal_7_result));
  equal equal_8 (.A(slt_result), .B({32{1'b0}}), .Result(equal_8_result));
  equal equal_9 (.A(sra_result), .B({32{1'b0}}), .Result(equal_9_result));
  equal equal_10 (.A(srl_result), .B({32{1'b0}}), .Result(equal_10_result));
  Multiplexer #(.select(4), .width(32)) multiplexer_1 (
    .in0(sub_result), .in1(add_result), .in2(mult_result), .in3(and_result), .in4(or_result),
    .in5(xor_result), .in6(sll_result), .in7(slt_result), .in8(sra_result), .in9(srl_result), .out(out_C),
    .sel(opcode[3:0]));  // open: in10, in11, in12, in13, in14, in15, en
  Multiplexer #(.select(4)) multiplexer_2 (
    .in0(sub_carry_out), .in1(add_carry_out), .in2(mult_carry_out), .in3(1'b0), .in4(1'b0), .in5(1'b0),
    .in6(1'b0), .in7(1'b0), .in8(1'b0), .in9(1'b0), .out(carryout), .sel(opcode[3:0]));  // open: in10, in11, in12, in13, in14, in15, en
  Multiplexer #(.select(4)) multiplexer_3 (
    .in0(equal_result), .in1(equal_2_result), .in2(equal_3_result), .in3(equal_4_result),
    .in4(equal_5_result), .in5(equal_6_result), .in6(equal_7_result), .in7(equal_8_result),
    .in8(equal_9_result), .in9(equal_10_result), .out(zero), .sel(opcode[3:0]));  // open: in10, in11, in12, in13, in14, in15, en
  Multiplexer #(.select(4)) multiplexer_4 (
    .in0(sub_overflow), .in1(add_overflow), .in2(mult_overflow), .in3(1'b0), .in4(1'b0), .in5(1'b0),
    .in6(1'b0), .in7(1'b0), .in8(1'b0), .in9(1'b0), .out(overflow), .sel(opcode[3:0]));  // open: in10, in11, in12, in13, in14, in15, en
endmodule

module one_bit_adder (
  input  A,
  input  B,
  input  Carry,
  output Sum,
  output Carry_Out
);

  wire and_1_out, and_2_out, xor_1_out;

  xor xor_1 (xor_1_out, A, B);
  xor xor_2 (Sum, xor_1_out, Carry);
  and and_1 (and_1_out, Carry, xor_1_out);
  and and_2 (and_2_out, A, B);
  or or_1 (Carry_Out, and_1_out, and_2_out);

  // Other names for the same wires on the sheet: C = Carry
endmodule

module \and  (
  input  [31:0] A,
  input  [31:0] B,
  output [31:0] Result
);

  assign Result = A & B;  // AND_Gate and_1, 32 bits wide
endmodule

module \or  (
  input  [31:0] A,
  input  [31:0] b,
  output [31:0] Result
);

  assign Result = A | b;  // OR_Gate or_1, 32 bits wide
endmodule

module \xor  (
  input  [31:0] A,
  input  [31:0] B,
  output [31:0] Result
);

  assign Result = A ^ B;  // XOR_Gate xor_1, 32 bits wide
endmodule

// ADD
module _32_bit_adder (
  input  [31:0] A,
  input  [31:0] B,
  output [31:0] Result,
  output carry_out,
  output overflow
);

  wire one_bit_adder_1_carry_out, one_bit_adder_2_carry_out, one_bit_adder_3_carry_out,
       one_bit_adder_4_carry_out, one_bit_adder_5_carry_out, one_bit_adder_6_carry_out,
       one_bit_adder_7_carry_out, one_bit_adder_8_carry_out, one_bit_adder_9_carry_out,
       one_bit_adder_10_carry_out, one_bit_adder_11_carry_out, one_bit_adder_12_carry_out,
       one_bit_adder_13_carry_out, one_bit_adder_14_carry_out, one_bit_adder_15_carry_out,
       one_bit_adder_16_carry_out, one_bit_adder_17_carry_out, one_bit_adder_18_carry_out,
       one_bit_adder_19_carry_out, one_bit_adder_20_carry_out, one_bit_adder_21_carry_out,
       one_bit_adder_22_carry_out, one_bit_adder_23_carry_out, one_bit_adder_24_carry_out,
       one_bit_adder_25_carry_out, one_bit_adder_26_carry_out, one_bit_adder_27_carry_out,
       one_bit_adder_28_carry_out, one_bit_adder_29_carry_out, one_bit_adder_30_carry_out,
       one_bit_adder_31_carry_out, xor_1_out, xor_2_out;

  one_bit_adder one_bit_adder_1 (
    .A(A[0]), .B(B[0]), .Carry(1'b0), .Carry_Out(one_bit_adder_1_carry_out), .Sum(Result[0]));
  one_bit_adder one_bit_adder_2 (
    .A(A[1]), .B(B[1]), .Carry(one_bit_adder_1_carry_out), .Carry_Out(one_bit_adder_2_carry_out),
    .Sum(Result[1]));
  one_bit_adder one_bit_adder_3 (
    .A(A[2]), .B(B[2]), .Carry(one_bit_adder_2_carry_out), .Carry_Out(one_bit_adder_3_carry_out),
    .Sum(Result[2]));
  one_bit_adder one_bit_adder_4 (
    .A(A[3]), .B(B[3]), .Carry(one_bit_adder_3_carry_out), .Carry_Out(one_bit_adder_4_carry_out),
    .Sum(Result[3]));
  one_bit_adder one_bit_adder_5 (
    .A(A[4]), .B(B[4]), .Carry(one_bit_adder_4_carry_out), .Carry_Out(one_bit_adder_5_carry_out),
    .Sum(Result[4]));
  one_bit_adder one_bit_adder_6 (
    .A(A[5]), .B(B[5]), .Carry(one_bit_adder_5_carry_out), .Carry_Out(one_bit_adder_6_carry_out),
    .Sum(Result[5]));
  one_bit_adder one_bit_adder_7 (
    .A(A[6]), .B(B[6]), .Carry(one_bit_adder_6_carry_out), .Carry_Out(one_bit_adder_7_carry_out),
    .Sum(Result[6]));
  one_bit_adder one_bit_adder_8 (
    .A(A[7]), .B(B[7]), .Carry(one_bit_adder_7_carry_out), .Carry_Out(one_bit_adder_8_carry_out),
    .Sum(Result[7]));
  one_bit_adder one_bit_adder_9 (
    .A(A[8]), .B(B[8]), .Carry(one_bit_adder_8_carry_out), .Carry_Out(one_bit_adder_9_carry_out),
    .Sum(Result[8]));
  one_bit_adder one_bit_adder_10 (
    .A(A[9]), .B(B[9]), .Carry(one_bit_adder_9_carry_out), .Carry_Out(one_bit_adder_10_carry_out),
    .Sum(Result[9]));
  one_bit_adder one_bit_adder_11 (
    .A(A[10]), .B(B[10]), .Carry(one_bit_adder_10_carry_out), .Carry_Out(one_bit_adder_11_carry_out),
    .Sum(Result[10]));
  one_bit_adder one_bit_adder_12 (
    .A(A[11]), .B(B[11]), .Carry(one_bit_adder_11_carry_out), .Carry_Out(one_bit_adder_12_carry_out),
    .Sum(Result[11]));
  one_bit_adder one_bit_adder_13 (
    .A(A[12]), .B(B[12]), .Carry(one_bit_adder_12_carry_out), .Carry_Out(one_bit_adder_13_carry_out),
    .Sum(Result[12]));
  one_bit_adder one_bit_adder_14 (
    .A(A[13]), .B(B[13]), .Carry(one_bit_adder_13_carry_out), .Carry_Out(one_bit_adder_14_carry_out),
    .Sum(Result[13]));
  one_bit_adder one_bit_adder_15 (
    .A(A[14]), .B(B[14]), .Carry(one_bit_adder_14_carry_out), .Carry_Out(one_bit_adder_15_carry_out),
    .Sum(Result[14]));
  one_bit_adder one_bit_adder_16 (
    .A(A[15]), .B(B[15]), .Carry(one_bit_adder_15_carry_out), .Carry_Out(one_bit_adder_16_carry_out),
    .Sum(Result[15]));
  one_bit_adder one_bit_adder_17 (
    .A(A[16]), .B(B[16]), .Carry(one_bit_adder_16_carry_out), .Carry_Out(one_bit_adder_17_carry_out),
    .Sum(Result[16]));
  one_bit_adder one_bit_adder_18 (
    .A(A[17]), .B(B[17]), .Carry(one_bit_adder_17_carry_out), .Carry_Out(one_bit_adder_18_carry_out),
    .Sum(Result[17]));
  one_bit_adder one_bit_adder_19 (
    .A(A[18]), .B(B[18]), .Carry(one_bit_adder_18_carry_out), .Carry_Out(one_bit_adder_19_carry_out),
    .Sum(Result[18]));
  one_bit_adder one_bit_adder_20 (
    .A(A[19]), .B(B[19]), .Carry(one_bit_adder_19_carry_out), .Carry_Out(one_bit_adder_20_carry_out),
    .Sum(Result[19]));
  one_bit_adder one_bit_adder_21 (
    .A(A[20]), .B(B[20]), .Carry(one_bit_adder_20_carry_out), .Carry_Out(one_bit_adder_21_carry_out),
    .Sum(Result[20]));
  one_bit_adder one_bit_adder_22 (
    .A(A[21]), .B(B[21]), .Carry(one_bit_adder_21_carry_out), .Carry_Out(one_bit_adder_22_carry_out),
    .Sum(Result[21]));
  one_bit_adder one_bit_adder_23 (
    .A(A[22]), .B(B[22]), .Carry(one_bit_adder_22_carry_out), .Carry_Out(one_bit_adder_23_carry_out),
    .Sum(Result[22]));
  one_bit_adder one_bit_adder_24 (
    .A(A[23]), .B(B[23]), .Carry(one_bit_adder_23_carry_out), .Carry_Out(one_bit_adder_24_carry_out),
    .Sum(Result[23]));
  one_bit_adder one_bit_adder_25 (
    .A(A[24]), .B(B[24]), .Carry(one_bit_adder_24_carry_out), .Carry_Out(one_bit_adder_25_carry_out),
    .Sum(Result[24]));
  one_bit_adder one_bit_adder_26 (
    .A(A[25]), .B(B[25]), .Carry(one_bit_adder_25_carry_out), .Carry_Out(one_bit_adder_26_carry_out),
    .Sum(Result[25]));
  one_bit_adder one_bit_adder_27 (
    .A(A[26]), .B(B[26]), .Carry(one_bit_adder_26_carry_out), .Carry_Out(one_bit_adder_27_carry_out),
    .Sum(Result[26]));
  one_bit_adder one_bit_adder_28 (
    .A(A[27]), .B(B[27]), .Carry(one_bit_adder_27_carry_out), .Carry_Out(one_bit_adder_28_carry_out),
    .Sum(Result[27]));
  one_bit_adder one_bit_adder_29 (
    .A(A[28]), .B(B[28]), .Carry(one_bit_adder_28_carry_out), .Carry_Out(one_bit_adder_29_carry_out),
    .Sum(Result[28]));
  one_bit_adder one_bit_adder_30 (
    .A(A[29]), .B(B[29]), .Carry(one_bit_adder_29_carry_out), .Carry_Out(one_bit_adder_30_carry_out),
    .Sum(Result[29]));
  one_bit_adder one_bit_adder_31 (
    .A(A[30]), .B(B[30]), .Carry(one_bit_adder_30_carry_out), .Carry_Out(one_bit_adder_31_carry_out),
    .Sum(Result[30]));
  one_bit_adder one_bit_adder_32 (
    .A(A[31]), .B(B[31]), .Carry(one_bit_adder_31_carry_out), .Carry_Out(carry_out), .Sum(Result[31]));
  xor xor_1 (xor_1_out, B[31], Result[31]);
  and and_1 (overflow, xor_1_out, xor_2_out);
  xor xor_2 (xor_2_out, A[31], Result[31]);

  // Other names for the same wires on the sheet: a_0 = A[0]; a_1 = A[1]; a_2 = A[2]; a_3 = A[3]; a_4 = A[4];
  //   a_5 = A[5]; a_6 = A[6]; a_7 = A[7]; a_8 = A[8]; a_9 = A[9]; a_10 = A[10]; a_11 = A[11]; a_12 = A[12];
  //   a_13 = A[13]; a_14 = A[14]; a_15 = A[15]; a_16 = A[16]; a_17 = A[17]; a_18 = A[18]; a_19 = A[19]; a_20 = A[20];
  //   a_21 = A[21]; a_22 = A[22]; a_23 = A[23]; a_24 = A[24]; a_25 = A[25]; a_26 = A[26]; a_27 = A[27]; a_28 = A[28];
  //   a_29 = A[29]; a_30 = A[30]; a_31 = A[31]; b_0 = B[0]; b_1 = B[1]; b_2 = B[2]; b_3 = B[3]; b_4 = B[4];
  //   b_5 = B[5]; b_6 = B[6]; b_7 = B[7]; b_8 = B[8]; b_9 = B[9]; b_10 = B[10]; b_11 = B[11]; b_12 = B[12];
  //   b_13 = B[13]; b_14 = B[14]; b_15 = B[15]; b_16 = B[16]; b_17 = B[17]; b_18 = B[18]; b_19 = B[19]; b_20 = B[20];
  //   b_21 = B[21]; b_22 = B[22]; b_23 = B[23]; b_24 = B[24]; b_25 = B[25]; b_26 = B[26]; b_27 = B[27]; b_28 = B[28];
  //   b_29 = B[29]; b_30 = B[30]; b_31 = B[31]; r_0 = Result[0]; r_1 = Result[1]; r_2 = Result[2]; r_3 = Result[3];
  //   r_4 = Result[4]; r_5 = Result[5]; r_6 = Result[6]; r_7 = Result[7]; r_8 = Result[8]; r_9 = Result[9];
  //   r_10 = Result[10]; r_11 = Result[11]; r_12 = Result[12]; r_13 = Result[13]; r_14 = Result[14];
  //   r_15 = Result[15]; r_16 = Result[16]; r_17 = Result[17]; r_18 = Result[18]; r_19 = Result[19];
  //   r_20 = Result[20]; r_21 = Result[21]; r_22 = Result[22]; r_23 = Result[23]; r_24 = Result[24];
  //   r_25 = Result[25]; r_26 = Result[26]; r_27 = Result[27]; r_28 = Result[28]; r_29 = Result[29];
  //   r_30 = Result[30]; r_31 = Result[31]
endmodule

module _32_bit_subs (
  input  [31:0] A,
  input  [31:0] B,
  output [31:0] Result,
  output overflow,
  output carry_out
);

  wire and_1_out, and_2_out, b_0, b_1, b_2, b_3, b_4, b_5, b_6, b_7, b_8, b_9, b_10, b_11, b_12, b_13, b_14,
       b_15, b_16, b_17, b_18, b_19, b_20, b_21, b_22, b_23, b_24, b_25, b_26, b_27, b_28, b_29, b_30, b_31,
       not_2_out, not_3_out, not_4_out, one_bit_adder_1_carry_out, one_bit_adder_2_carry_out,
       one_bit_adder_3_carry_out, one_bit_adder_4_carry_out, one_bit_adder_5_carry_out,
       one_bit_adder_6_carry_out, one_bit_adder_7_carry_out, one_bit_adder_8_carry_out,
       one_bit_adder_9_carry_out, one_bit_adder_10_carry_out, one_bit_adder_11_carry_out,
       one_bit_adder_12_carry_out, one_bit_adder_13_carry_out, one_bit_adder_14_carry_out,
       one_bit_adder_15_carry_out, one_bit_adder_16_carry_out, one_bit_adder_17_carry_out,
       one_bit_adder_18_carry_out, one_bit_adder_19_carry_out, one_bit_adder_20_carry_out,
       one_bit_adder_21_carry_out, one_bit_adder_22_carry_out, one_bit_adder_23_carry_out,
       one_bit_adder_24_carry_out, one_bit_adder_25_carry_out, one_bit_adder_26_carry_out,
       one_bit_adder_27_carry_out, one_bit_adder_28_carry_out, one_bit_adder_29_carry_out,
       one_bit_adder_30_carry_out, one_bit_adder_31_carry_out;

  assign {b_31, b_30, b_29, b_28, b_27, b_26, b_25, b_24, b_23, b_22, b_21, b_20, b_19, b_18, b_17, b_16, b_15, b_14, b_13, b_12, b_11, b_10, b_9, b_8, b_7, b_6, b_5, b_4, b_3, b_2, b_1, b_0} = ~B;  // NOT_Gate not_1, 32 bits wide
  one_bit_adder one_bit_adder_1 (
    .A(A[0]), .B(b_0), .Carry(1'b1), .Carry_Out(one_bit_adder_1_carry_out), .Sum(Result[0]));
  one_bit_adder one_bit_adder_2 (
    .A(A[1]), .B(b_1), .Carry(one_bit_adder_1_carry_out), .Carry_Out(one_bit_adder_2_carry_out),
    .Sum(Result[1]));
  one_bit_adder one_bit_adder_3 (
    .A(A[2]), .B(b_2), .Carry(one_bit_adder_2_carry_out), .Carry_Out(one_bit_adder_3_carry_out),
    .Sum(Result[2]));
  one_bit_adder one_bit_adder_4 (
    .A(A[3]), .B(b_3), .Carry(one_bit_adder_3_carry_out), .Carry_Out(one_bit_adder_4_carry_out),
    .Sum(Result[3]));
  one_bit_adder one_bit_adder_5 (
    .A(A[4]), .B(b_4), .Carry(one_bit_adder_4_carry_out), .Carry_Out(one_bit_adder_5_carry_out),
    .Sum(Result[4]));
  one_bit_adder one_bit_adder_6 (
    .A(A[5]), .B(b_5), .Carry(one_bit_adder_5_carry_out), .Carry_Out(one_bit_adder_6_carry_out),
    .Sum(Result[5]));
  one_bit_adder one_bit_adder_7 (
    .A(A[6]), .B(b_6), .Carry(one_bit_adder_6_carry_out), .Carry_Out(one_bit_adder_7_carry_out),
    .Sum(Result[6]));
  one_bit_adder one_bit_adder_8 (
    .A(A[7]), .B(b_7), .Carry(one_bit_adder_7_carry_out), .Carry_Out(one_bit_adder_8_carry_out),
    .Sum(Result[7]));
  one_bit_adder one_bit_adder_9 (
    .A(A[8]), .B(b_8), .Carry(one_bit_adder_8_carry_out), .Carry_Out(one_bit_adder_9_carry_out),
    .Sum(Result[8]));
  one_bit_adder one_bit_adder_10 (
    .A(A[9]), .B(b_9), .Carry(one_bit_adder_9_carry_out), .Carry_Out(one_bit_adder_10_carry_out),
    .Sum(Result[9]));
  one_bit_adder one_bit_adder_11 (
    .A(A[10]), .B(b_10), .Carry(one_bit_adder_10_carry_out), .Carry_Out(one_bit_adder_11_carry_out),
    .Sum(Result[10]));
  one_bit_adder one_bit_adder_12 (
    .A(A[11]), .B(b_11), .Carry(one_bit_adder_11_carry_out), .Carry_Out(one_bit_adder_12_carry_out),
    .Sum(Result[11]));
  one_bit_adder one_bit_adder_13 (
    .A(A[12]), .B(b_12), .Carry(one_bit_adder_12_carry_out), .Carry_Out(one_bit_adder_13_carry_out),
    .Sum(Result[12]));
  one_bit_adder one_bit_adder_14 (
    .A(A[13]), .B(b_13), .Carry(one_bit_adder_13_carry_out), .Carry_Out(one_bit_adder_14_carry_out),
    .Sum(Result[13]));
  one_bit_adder one_bit_adder_15 (
    .A(A[14]), .B(b_14), .Carry(one_bit_adder_14_carry_out), .Carry_Out(one_bit_adder_15_carry_out),
    .Sum(Result[14]));
  one_bit_adder one_bit_adder_16 (
    .A(A[15]), .B(b_15), .Carry(one_bit_adder_15_carry_out), .Carry_Out(one_bit_adder_16_carry_out),
    .Sum(Result[15]));
  one_bit_adder one_bit_adder_17 (
    .A(A[16]), .B(b_16), .Carry(one_bit_adder_16_carry_out), .Carry_Out(one_bit_adder_17_carry_out),
    .Sum(Result[16]));
  one_bit_adder one_bit_adder_18 (
    .A(A[17]), .B(b_17), .Carry(one_bit_adder_17_carry_out), .Carry_Out(one_bit_adder_18_carry_out),
    .Sum(Result[17]));
  one_bit_adder one_bit_adder_19 (
    .A(A[18]), .B(b_18), .Carry(one_bit_adder_18_carry_out), .Carry_Out(one_bit_adder_19_carry_out),
    .Sum(Result[18]));
  one_bit_adder one_bit_adder_20 (
    .A(A[19]), .B(b_19), .Carry(one_bit_adder_19_carry_out), .Carry_Out(one_bit_adder_20_carry_out),
    .Sum(Result[19]));
  one_bit_adder one_bit_adder_21 (
    .A(A[20]), .B(b_20), .Carry(one_bit_adder_20_carry_out), .Carry_Out(one_bit_adder_21_carry_out),
    .Sum(Result[20]));
  one_bit_adder one_bit_adder_22 (
    .A(A[21]), .B(b_21), .Carry(one_bit_adder_21_carry_out), .Carry_Out(one_bit_adder_22_carry_out),
    .Sum(Result[21]));
  one_bit_adder one_bit_adder_23 (
    .A(A[22]), .B(b_22), .Carry(one_bit_adder_22_carry_out), .Carry_Out(one_bit_adder_23_carry_out),
    .Sum(Result[22]));
  one_bit_adder one_bit_adder_24 (
    .A(A[23]), .B(b_23), .Carry(one_bit_adder_23_carry_out), .Carry_Out(one_bit_adder_24_carry_out),
    .Sum(Result[23]));
  one_bit_adder one_bit_adder_25 (
    .A(A[24]), .B(b_24), .Carry(one_bit_adder_24_carry_out), .Carry_Out(one_bit_adder_25_carry_out),
    .Sum(Result[24]));
  one_bit_adder one_bit_adder_26 (
    .A(A[25]), .B(b_25), .Carry(one_bit_adder_25_carry_out), .Carry_Out(one_bit_adder_26_carry_out),
    .Sum(Result[25]));
  one_bit_adder one_bit_adder_27 (
    .A(A[26]), .B(b_26), .Carry(one_bit_adder_26_carry_out), .Carry_Out(one_bit_adder_27_carry_out),
    .Sum(Result[26]));
  one_bit_adder one_bit_adder_28 (
    .A(A[27]), .B(b_27), .Carry(one_bit_adder_27_carry_out), .Carry_Out(one_bit_adder_28_carry_out),
    .Sum(Result[27]));
  one_bit_adder one_bit_adder_29 (
    .A(A[28]), .B(b_28), .Carry(one_bit_adder_28_carry_out), .Carry_Out(one_bit_adder_29_carry_out),
    .Sum(Result[28]));
  one_bit_adder one_bit_adder_30 (
    .A(A[29]), .B(b_29), .Carry(one_bit_adder_29_carry_out), .Carry_Out(one_bit_adder_30_carry_out),
    .Sum(Result[29]));
  one_bit_adder one_bit_adder_31 (
    .A(A[30]), .B(b_30), .Carry(one_bit_adder_30_carry_out), .Carry_Out(one_bit_adder_31_carry_out),
    .Sum(Result[30]));
  one_bit_adder one_bit_adder_32 (
    .A(A[31]), .B(b_31), .Carry(one_bit_adder_31_carry_out), .Carry_Out(carry_out), .Sum(Result[31]));
  not not_2 (not_2_out, B[31]);
  and and_1 (and_1_out, A[31], not_2_out, not_3_out);
  not not_3 (not_3_out, Result[31]);
  or or_1 (overflow, and_1_out, and_2_out);
  not not_4 (not_4_out, A[31]);
  and and_2 (and_2_out, not_4_out, B[31], Result[31]);

  // Other names for the same wires on the sheet: a_0 = A[0]; a_1 = A[1]; a_2 = A[2]; a_3 = A[3]; a_4 = A[4];
  //   a_5 = A[5]; a_6 = A[6]; a_7 = A[7]; a_8 = A[8]; a_9 = A[9]; a_10 = A[10]; a_11 = A[11]; a_12 = A[12];
  //   a_13 = A[13]; a_14 = A[14]; a_15 = A[15]; a_16 = A[16]; a_17 = A[17]; a_18 = A[18]; a_19 = A[19]; a_20 = A[20];
  //   a_21 = A[21]; a_22 = A[22]; a_23 = A[23]; a_24 = A[24]; a_25 = A[25]; a_26 = A[26]; a_27 = A[27]; a_28 = A[28];
  //   a_29 = A[29]; a_30 = A[30]; a_31 = A[31]; in_B_31 = B[31]; r_0 = Result[0]; r_1 = Result[1]; r_2 = Result[2];
  //   r_3 = Result[3]; r_4 = Result[4]; r_5 = Result[5]; r_6 = Result[6]; r_7 = Result[7]; r_8 = Result[8];
  //   r_9 = Result[9]; r_10 = Result[10]; r_11 = Result[11]; r_12 = Result[12]; r_13 = Result[13]; r_14 = Result[14];
  //   r_15 = Result[15]; r_16 = Result[16]; r_17 = Result[17]; r_18 = Result[18]; r_19 = Result[19];
  //   r_20 = Result[20]; r_21 = Result[21]; r_22 = Result[22]; r_23 = Result[23]; r_24 = Result[24];
  //   r_25 = Result[25]; r_26 = Result[26]; r_27 = Result[27]; r_28 = Result[28]; r_29 = Result[29];
  //   r_30 = Result[30]; r_31 = Result[31]
endmodule

module shift_left (
  input  [31:0] A,
  input  [31:0] B,
  output [31:0] Result
);

  wire [1:0] multiplexer_2_out, multiplexer_4_out, multiplexer_6_out, multiplexer_8_out, multiplexer_10_out,
       multiplexer_12_out, multiplexer_14_out, multiplexer_16_out, multiplexer_18_out, multiplexer_20_out,
       multiplexer_22_out, multiplexer_24_out, multiplexer_26_out, multiplexer_28_out, multiplexer_30_out,
       multiplexer_32_out, multiplexer_33_out, multiplexer_34_out, multiplexer_35_out, multiplexer_36_out,
       multiplexer_37_out, multiplexer_38_out, multiplexer_39_out, multiplexer_40_out, multiplexer_41_out,
       multiplexer_42_out, multiplexer_43_out, multiplexer_44_out, multiplexer_45_out, multiplexer_46_out,
       multiplexer_47_out, multiplexer_48_out;
  wire [3:0] multiplexer_49_out, multiplexer_50_out, multiplexer_51_out, multiplexer_52_out,
       multiplexer_53_out, multiplexer_54_out, multiplexer_55_out, multiplexer_56_out;
  wire [7:0] multiplexer_57_out, multiplexer_58_out, multiplexer_59_out, multiplexer_60_out;

  Multiplexer multiplexer_1 (.in0(A[31]), .in1(A[30]), .out(multiplexer_2_out[1]), .sel(B[0]));  // open: en
  Multiplexer multiplexer_2 (.in0(A[30]), .in1(A[29]), .out(multiplexer_2_out[0]), .sel(B[0]));  // open: en
  Multiplexer multiplexer_3 (.in0(A[29]), .in1(A[28]), .out(multiplexer_4_out[1]), .sel(B[0]));  // open: en
  Multiplexer multiplexer_4 (.in0(A[28]), .in1(A[27]), .out(multiplexer_4_out[0]), .sel(B[0]));  // open: en
  Multiplexer multiplexer_5 (.in0(A[27]), .in1(A[26]), .out(multiplexer_6_out[1]), .sel(B[0]));  // open: en
  Multiplexer multiplexer_6 (.in0(A[26]), .in1(A[25]), .out(multiplexer_6_out[0]), .sel(B[0]));  // open: en
  Multiplexer multiplexer_7 (.in0(A[25]), .in1(A[24]), .out(multiplexer_8_out[1]), .sel(B[0]));  // open: en
  Multiplexer multiplexer_8 (.in0(A[24]), .in1(A[23]), .out(multiplexer_8_out[0]), .sel(B[0]));  // open: en
  Multiplexer multiplexer_9 (.in0(A[23]), .in1(A[22]), .out(multiplexer_10_out[1]), .sel(B[0]));  // open: en
  Multiplexer multiplexer_10 (.in0(A[22]), .in1(A[21]), .out(multiplexer_10_out[0]), .sel(B[0]));  // open: en
  Multiplexer multiplexer_11 (.in0(A[21]), .in1(A[20]), .out(multiplexer_12_out[1]), .sel(B[0]));  // open: en
  Multiplexer multiplexer_12 (.in0(A[20]), .in1(A[19]), .out(multiplexer_12_out[0]), .sel(B[0]));  // open: en
  Multiplexer multiplexer_13 (.in0(A[19]), .in1(A[18]), .out(multiplexer_14_out[1]), .sel(B[0]));  // open: en
  Multiplexer multiplexer_14 (.in0(A[18]), .in1(A[17]), .out(multiplexer_14_out[0]), .sel(B[0]));  // open: en
  Multiplexer multiplexer_15 (.in0(A[17]), .in1(A[16]), .out(multiplexer_16_out[1]), .sel(B[0]));  // open: en
  Multiplexer multiplexer_16 (.in0(A[16]), .in1(A[15]), .out(multiplexer_16_out[0]), .sel(B[0]));  // open: en
  Multiplexer multiplexer_17 (.in0(A[15]), .in1(A[14]), .out(multiplexer_18_out[1]), .sel(B[0]));  // open: en
  Multiplexer multiplexer_18 (.in0(A[14]), .in1(A[13]), .out(multiplexer_18_out[0]), .sel(B[0]));  // open: en
  Multiplexer multiplexer_19 (.in0(A[13]), .in1(A[12]), .out(multiplexer_20_out[1]), .sel(B[0]));  // open: en
  Multiplexer multiplexer_20 (.in0(A[12]), .in1(A[11]), .out(multiplexer_20_out[0]), .sel(B[0]));  // open: en
  Multiplexer multiplexer_21 (.in0(A[11]), .in1(A[10]), .out(multiplexer_22_out[1]), .sel(B[0]));  // open: en
  Multiplexer multiplexer_22 (.in0(A[10]), .in1(A[9]), .out(multiplexer_22_out[0]), .sel(B[0]));  // open: en
  Multiplexer multiplexer_23 (.in0(A[9]), .in1(A[8]), .out(multiplexer_24_out[1]), .sel(B[0]));  // open: en
  Multiplexer multiplexer_24 (.in0(A[8]), .in1(A[7]), .out(multiplexer_24_out[0]), .sel(B[0]));  // open: en
  Multiplexer multiplexer_25 (.in0(A[7]), .in1(A[6]), .out(multiplexer_26_out[1]), .sel(B[0]));  // open: en
  Multiplexer multiplexer_26 (.in0(A[6]), .in1(A[5]), .out(multiplexer_26_out[0]), .sel(B[0]));  // open: en
  Multiplexer multiplexer_27 (.in0(A[5]), .in1(A[4]), .out(multiplexer_28_out[1]), .sel(B[0]));  // open: en
  Multiplexer multiplexer_28 (.in0(A[4]), .in1(A[3]), .out(multiplexer_28_out[0]), .sel(B[0]));  // open: en
  Multiplexer multiplexer_29 (.in0(A[3]), .in1(A[2]), .out(multiplexer_30_out[1]), .sel(B[0]));  // open: en
  Multiplexer multiplexer_30 (.in0(A[2]), .in1(A[1]), .out(multiplexer_30_out[0]), .sel(B[0]));  // open: en
  Multiplexer multiplexer_31 (.in0(A[1]), .in1(A[0]), .out(multiplexer_32_out[1]), .sel(B[0]));  // open: en
  Multiplexer multiplexer_32 (.in0(A[0]), .in1(1'b0), .out(multiplexer_32_out[0]), .sel(B[0]));  // open: en
  Multiplexer #(.width(2)) multiplexer_33 (
    .in0(multiplexer_2_out), .in1(multiplexer_4_out), .out(multiplexer_33_out), .sel(B[1]));  // open: en
  Multiplexer #(.width(2)) multiplexer_34 (
    .in0(multiplexer_4_out), .in1(multiplexer_6_out), .out(multiplexer_34_out), .sel(B[1]));  // open: en
  Multiplexer #(.width(2)) multiplexer_35 (
    .in0(multiplexer_6_out), .in1(multiplexer_8_out), .out(multiplexer_35_out), .sel(B[1]));  // open: en
  Multiplexer #(.width(2)) multiplexer_36 (
    .in0(multiplexer_8_out), .in1(multiplexer_10_out), .out(multiplexer_36_out), .sel(B[1]));  // open: en
  Multiplexer #(.width(2)) multiplexer_37 (
    .in0(multiplexer_10_out), .in1(multiplexer_12_out), .out(multiplexer_37_out), .sel(B[1]));  // open: en
  Multiplexer #(.width(2)) multiplexer_38 (
    .in0(multiplexer_12_out), .in1(multiplexer_14_out), .out(multiplexer_38_out), .sel(B[1]));  // open: en
  Multiplexer #(.width(2)) multiplexer_39 (
    .in0(multiplexer_14_out), .in1(multiplexer_16_out), .out(multiplexer_39_out), .sel(B[1]));  // open: en
  Multiplexer #(.width(2)) multiplexer_40 (
    .in0(multiplexer_16_out), .in1(multiplexer_18_out), .out(multiplexer_40_out), .sel(B[1]));  // open: en
  Multiplexer #(.width(2)) multiplexer_41 (
    .in0(multiplexer_18_out), .in1(multiplexer_20_out), .out(multiplexer_41_out), .sel(B[1]));  // open: en
  Multiplexer #(.width(2)) multiplexer_42 (
    .in0(multiplexer_20_out), .in1(multiplexer_22_out), .out(multiplexer_42_out), .sel(B[1]));  // open: en
  Multiplexer #(.width(2)) multiplexer_43 (
    .in0(multiplexer_22_out), .in1(multiplexer_24_out), .out(multiplexer_43_out), .sel(B[1]));  // open: en
  Multiplexer #(.width(2)) multiplexer_44 (
    .in0(multiplexer_24_out), .in1(multiplexer_26_out), .out(multiplexer_44_out), .sel(B[1]));  // open: en
  Multiplexer #(.width(2)) multiplexer_45 (
    .in0(multiplexer_26_out), .in1(multiplexer_28_out), .out(multiplexer_45_out), .sel(B[1]));  // open: en
  Multiplexer #(.width(2)) multiplexer_46 (
    .in0(multiplexer_28_out), .in1(multiplexer_30_out), .out(multiplexer_46_out), .sel(B[1]));  // open: en
  Multiplexer #(.width(2)) multiplexer_47 (
    .in0(multiplexer_30_out), .in1(multiplexer_32_out), .out(multiplexer_47_out), .sel(B[1]));  // open: en
  Multiplexer #(.width(2)) multiplexer_48 (
    .in0(multiplexer_32_out), .in1(2'b00), .out(multiplexer_48_out), .sel(B[1]));  // open: en
  Multiplexer #(.width(4)) multiplexer_49 (
    .in0({multiplexer_33_out, multiplexer_34_out}), .in1({multiplexer_35_out, multiplexer_36_out}),
    .out(multiplexer_49_out), .sel(B[2]));  // open: en
  Multiplexer #(.width(4)) multiplexer_50 (
    .in0({multiplexer_35_out, multiplexer_36_out}), .in1({multiplexer_37_out, multiplexer_38_out}),
    .out(multiplexer_50_out), .sel(B[2]));  // open: en
  Multiplexer #(.width(4)) multiplexer_51 (
    .in0({multiplexer_37_out, multiplexer_38_out}), .in1({multiplexer_39_out, multiplexer_40_out}),
    .out(multiplexer_51_out), .sel(B[2]));  // open: en
  Multiplexer #(.width(4)) multiplexer_52 (
    .in0({multiplexer_39_out, multiplexer_40_out}), .in1({multiplexer_41_out, multiplexer_42_out}),
    .out(multiplexer_52_out), .sel(B[2]));  // open: en
  Multiplexer #(.width(4)) multiplexer_53 (
    .in0({multiplexer_41_out, multiplexer_42_out}), .in1({multiplexer_43_out, multiplexer_44_out}),
    .out(multiplexer_53_out), .sel(B[2]));  // open: en
  Multiplexer #(.width(4)) multiplexer_54 (
    .in0({multiplexer_43_out, multiplexer_44_out}), .in1({multiplexer_45_out, multiplexer_46_out}),
    .out(multiplexer_54_out), .sel(B[2]));  // open: en
  Multiplexer #(.width(4)) multiplexer_55 (
    .in0({multiplexer_45_out, multiplexer_46_out}), .in1({multiplexer_47_out, multiplexer_48_out}),
    .out(multiplexer_55_out), .sel(B[2]));  // open: en
  Multiplexer #(.width(4)) multiplexer_56 (
    .in0({multiplexer_47_out, multiplexer_48_out}), .in1(4'b0000), .out(multiplexer_56_out), .sel(B[2]));  // open: en
  Multiplexer #(.width(8)) multiplexer_57 (
    .in0({multiplexer_49_out, multiplexer_50_out}), .in1({multiplexer_51_out, multiplexer_52_out}),
    .out(multiplexer_57_out), .sel(B[3]));  // open: en
  Multiplexer #(.width(8)) multiplexer_58 (
    .in0({multiplexer_51_out, multiplexer_52_out}), .in1({multiplexer_53_out, multiplexer_54_out}),
    .out(multiplexer_58_out), .sel(B[3]));  // open: en
  Multiplexer #(.width(8)) multiplexer_59 (
    .in0({multiplexer_53_out, multiplexer_54_out}), .in1({multiplexer_55_out, multiplexer_56_out}),
    .out(multiplexer_59_out), .sel(B[3]));  // open: en
  Multiplexer #(.width(8)) multiplexer_60 (
    .in0({multiplexer_55_out, multiplexer_56_out}), .in1({8{1'b0}}), .out(multiplexer_60_out), .sel(B[3]));  // open: en
  Multiplexer #(.width(16)) multiplexer_61 (
    .in0({multiplexer_57_out, multiplexer_58_out}), .in1({multiplexer_59_out, multiplexer_60_out}),
    .out(Result[31:16]), .sel(B[4]));  // open: en
  Multiplexer #(.width(16)) multiplexer_62 (
    .in0({multiplexer_59_out, multiplexer_60_out}), .in1({16{1'b0}}), .out(Result[15:0]), .sel(B[4]));  // open: en

  // Other names for the same wires on the sheet: b_0 = B[0]; b_1 = B[1]; b_2 = B[2]; b_3 = B[3]; b_4 = B[4]
endmodule

module set_less_than (
  input  [31:0] A,
  input  [31:0] B,
  output [31:0] Result
);

  wire n32_bit_subs_1_carry_out, not_1_out;

  _32_bit_subs u_32_bit_subs_1 (.A(A), .B(B), .carry_out(n32_bit_subs_1_carry_out));  // open: overflow, Result
  not not_1 (not_1_out, n32_bit_subs_1_carry_out);
  assign Result = {{31{1'b0}}, not_1_out};  // Bit_Extender bit_extender_1
endmodule

module shift_logical_right (
  input  [31:0] A,
  input  [31:0] B,
  output [31:0] Result
);

  wire [1:0] multiplexer_1_out, multiplexer_3_out, multiplexer_5_out, multiplexer_7_out, multiplexer_9_out,
       multiplexer_11_out, multiplexer_13_out, multiplexer_15_out, multiplexer_17_out, multiplexer_19_out,
       multiplexer_21_out, multiplexer_23_out, multiplexer_25_out, multiplexer_27_out, multiplexer_29_out,
       multiplexer_31_out, multiplexer_33_out, multiplexer_34_out, multiplexer_35_out, multiplexer_36_out,
       multiplexer_37_out, multiplexer_38_out, multiplexer_39_out, multiplexer_40_out, multiplexer_41_out,
       multiplexer_42_out, multiplexer_43_out, multiplexer_44_out, multiplexer_45_out, multiplexer_46_out,
       multiplexer_47_out, multiplexer_48_out;
  wire [3:0] multiplexer_49_out, multiplexer_50_out, multiplexer_51_out, multiplexer_52_out,
       multiplexer_53_out, multiplexer_54_out, multiplexer_55_out, multiplexer_56_out;
  wire [7:0] multiplexer_57_out, multiplexer_58_out, multiplexer_59_out, multiplexer_60_out;

  Multiplexer multiplexer_1 (.in0(A[0]), .in1(A[1]), .out(multiplexer_1_out[0]), .sel(B[0]));  // open: en
  Multiplexer multiplexer_2 (.in0(A[1]), .in1(A[2]), .out(multiplexer_1_out[1]), .sel(B[0]));  // open: en
  Multiplexer multiplexer_3 (.in0(A[2]), .in1(A[3]), .out(multiplexer_3_out[0]), .sel(B[0]));  // open: en
  Multiplexer multiplexer_4 (.in0(A[3]), .in1(A[4]), .out(multiplexer_3_out[1]), .sel(B[0]));  // open: en
  Multiplexer multiplexer_5 (.in0(A[4]), .in1(A[5]), .out(multiplexer_5_out[0]), .sel(B[0]));  // open: en
  Multiplexer multiplexer_6 (.in0(A[5]), .in1(A[6]), .out(multiplexer_5_out[1]), .sel(B[0]));  // open: en
  Multiplexer multiplexer_7 (.in0(A[6]), .in1(A[7]), .out(multiplexer_7_out[0]), .sel(B[0]));  // open: en
  Multiplexer multiplexer_8 (.in0(A[7]), .in1(A[8]), .out(multiplexer_7_out[1]), .sel(B[0]));  // open: en
  Multiplexer multiplexer_9 (.in0(A[8]), .in1(A[9]), .out(multiplexer_9_out[0]), .sel(B[0]));  // open: en
  Multiplexer multiplexer_10 (.in0(A[9]), .in1(A[10]), .out(multiplexer_9_out[1]), .sel(B[0]));  // open: en
  Multiplexer multiplexer_11 (.in0(A[10]), .in1(A[11]), .out(multiplexer_11_out[0]), .sel(B[0]));  // open: en
  Multiplexer multiplexer_12 (.in0(A[11]), .in1(A[12]), .out(multiplexer_11_out[1]), .sel(B[0]));  // open: en
  Multiplexer multiplexer_13 (.in0(A[12]), .in1(A[13]), .out(multiplexer_13_out[0]), .sel(B[0]));  // open: en
  Multiplexer multiplexer_14 (.in0(A[13]), .in1(A[14]), .out(multiplexer_13_out[1]), .sel(B[0]));  // open: en
  Multiplexer multiplexer_15 (.in0(A[14]), .in1(A[15]), .out(multiplexer_15_out[0]), .sel(B[0]));  // open: en
  Multiplexer multiplexer_16 (.in0(A[15]), .in1(A[16]), .out(multiplexer_15_out[1]), .sel(B[0]));  // open: en
  Multiplexer multiplexer_17 (.in0(A[16]), .in1(A[17]), .out(multiplexer_17_out[0]), .sel(B[0]));  // open: en
  Multiplexer multiplexer_18 (.in0(A[17]), .in1(A[18]), .out(multiplexer_17_out[1]), .sel(B[0]));  // open: en
  Multiplexer multiplexer_19 (.in0(A[18]), .in1(A[19]), .out(multiplexer_19_out[0]), .sel(B[0]));  // open: en
  Multiplexer multiplexer_20 (.in0(A[19]), .in1(A[20]), .out(multiplexer_19_out[1]), .sel(B[0]));  // open: en
  Multiplexer multiplexer_21 (.in0(A[20]), .in1(A[21]), .out(multiplexer_21_out[0]), .sel(B[0]));  // open: en
  Multiplexer multiplexer_22 (.in0(A[21]), .in1(A[22]), .out(multiplexer_21_out[1]), .sel(B[0]));  // open: en
  Multiplexer multiplexer_23 (.in0(A[22]), .in1(A[23]), .out(multiplexer_23_out[0]), .sel(B[0]));  // open: en
  Multiplexer multiplexer_24 (.in0(A[23]), .in1(A[24]), .out(multiplexer_23_out[1]), .sel(B[0]));  // open: en
  Multiplexer multiplexer_25 (.in0(A[24]), .in1(A[25]), .out(multiplexer_25_out[0]), .sel(B[0]));  // open: en
  Multiplexer multiplexer_26 (.in0(A[25]), .in1(A[26]), .out(multiplexer_25_out[1]), .sel(B[0]));  // open: en
  Multiplexer multiplexer_27 (.in0(A[26]), .in1(A[27]), .out(multiplexer_27_out[0]), .sel(B[0]));  // open: en
  Multiplexer multiplexer_28 (.in0(A[27]), .in1(A[28]), .out(multiplexer_27_out[1]), .sel(B[0]));  // open: en
  Multiplexer multiplexer_29 (.in0(A[28]), .in1(A[29]), .out(multiplexer_29_out[0]), .sel(B[0]));  // open: en
  Multiplexer multiplexer_30 (.in0(A[29]), .in1(A[30]), .out(multiplexer_29_out[1]), .sel(B[0]));  // open: en
  Multiplexer multiplexer_31 (.in0(A[30]), .in1(A[31]), .out(multiplexer_31_out[0]), .sel(B[0]));  // open: en
  Multiplexer multiplexer_32 (.in0(A[31]), .in1(1'b0), .out(multiplexer_31_out[1]), .sel(B[0]));  // open: en
  Multiplexer #(.width(2)) multiplexer_33 (
    .in0(multiplexer_1_out), .in1(multiplexer_3_out), .out(multiplexer_33_out), .sel(B[1]));  // open: en
  Multiplexer #(.width(2)) multiplexer_34 (
    .in0(multiplexer_3_out), .in1(multiplexer_5_out), .out(multiplexer_34_out), .sel(B[1]));  // open: en
  Multiplexer #(.width(2)) multiplexer_35 (
    .in0(multiplexer_5_out), .in1(multiplexer_7_out), .out(multiplexer_35_out), .sel(B[1]));  // open: en
  Multiplexer #(.width(2)) multiplexer_36 (
    .in0(multiplexer_7_out), .in1(multiplexer_9_out), .out(multiplexer_36_out), .sel(B[1]));  // open: en
  Multiplexer #(.width(2)) multiplexer_37 (
    .in0(multiplexer_9_out), .in1(multiplexer_11_out), .out(multiplexer_37_out), .sel(B[1]));  // open: en
  Multiplexer #(.width(2)) multiplexer_38 (
    .in0(multiplexer_11_out), .in1(multiplexer_13_out), .out(multiplexer_38_out), .sel(B[1]));  // open: en
  Multiplexer #(.width(2)) multiplexer_39 (
    .in0(multiplexer_13_out), .in1(multiplexer_15_out), .out(multiplexer_39_out), .sel(B[1]));  // open: en
  Multiplexer #(.width(2)) multiplexer_40 (
    .in0(multiplexer_15_out), .in1(multiplexer_17_out), .out(multiplexer_40_out), .sel(B[1]));  // open: en
  Multiplexer #(.width(2)) multiplexer_41 (
    .in0(multiplexer_17_out), .in1(multiplexer_19_out), .out(multiplexer_41_out), .sel(B[1]));  // open: en
  Multiplexer #(.width(2)) multiplexer_42 (
    .in0(multiplexer_19_out), .in1(multiplexer_21_out), .out(multiplexer_42_out), .sel(B[1]));  // open: en
  Multiplexer #(.width(2)) multiplexer_43 (
    .in0(multiplexer_21_out), .in1(multiplexer_23_out), .out(multiplexer_43_out), .sel(B[1]));  // open: en
  Multiplexer #(.width(2)) multiplexer_44 (
    .in0(multiplexer_23_out), .in1(multiplexer_25_out), .out(multiplexer_44_out), .sel(B[1]));  // open: en
  Multiplexer #(.width(2)) multiplexer_45 (
    .in0(multiplexer_25_out), .in1(multiplexer_27_out), .out(multiplexer_45_out), .sel(B[1]));  // open: en
  Multiplexer #(.width(2)) multiplexer_46 (
    .in0(multiplexer_27_out), .in1(multiplexer_29_out), .out(multiplexer_46_out), .sel(B[1]));  // open: en
  Multiplexer #(.width(2)) multiplexer_47 (
    .in0(multiplexer_29_out), .in1(multiplexer_31_out), .out(multiplexer_47_out), .sel(B[1]));  // open: en
  Multiplexer #(.width(2)) multiplexer_48 (
    .in0(multiplexer_31_out), .in1(2'b00), .out(multiplexer_48_out), .sel(B[1]));  // open: en
  Multiplexer #(.width(4)) multiplexer_49 (
    .in0({multiplexer_34_out, multiplexer_33_out}), .in1({multiplexer_36_out, multiplexer_35_out}),
    .out(multiplexer_49_out), .sel(B[2]));  // open: en
  Multiplexer #(.width(4)) multiplexer_50 (
    .in0({multiplexer_36_out, multiplexer_35_out}), .in1({multiplexer_38_out, multiplexer_37_out}),
    .out(multiplexer_50_out), .sel(B[2]));  // open: en
  Multiplexer #(.width(4)) multiplexer_51 (
    .in0({multiplexer_38_out, multiplexer_37_out}), .in1({multiplexer_40_out, multiplexer_39_out}),
    .out(multiplexer_51_out), .sel(B[2]));  // open: en
  Multiplexer #(.width(4)) multiplexer_52 (
    .in0({multiplexer_40_out, multiplexer_39_out}), .in1({multiplexer_42_out, multiplexer_41_out}),
    .out(multiplexer_52_out), .sel(B[2]));  // open: en
  Multiplexer #(.width(4)) multiplexer_53 (
    .in0({multiplexer_42_out, multiplexer_41_out}), .in1({multiplexer_44_out, multiplexer_43_out}),
    .out(multiplexer_53_out), .sel(B[2]));  // open: en
  Multiplexer #(.width(4)) multiplexer_54 (
    .in0({multiplexer_44_out, multiplexer_43_out}), .in1({multiplexer_46_out, multiplexer_45_out}),
    .out(multiplexer_54_out), .sel(B[2]));  // open: en
  Multiplexer #(.width(4)) multiplexer_55 (
    .in0({multiplexer_46_out, multiplexer_45_out}), .in1({multiplexer_48_out, multiplexer_47_out}),
    .out(multiplexer_55_out), .sel(B[2]));  // open: en
  Multiplexer #(.width(4)) multiplexer_56 (
    .in0({multiplexer_48_out, multiplexer_47_out}), .in1(4'b0000), .out(multiplexer_56_out), .sel(B[2]));  // open: en
  Multiplexer #(.width(8)) multiplexer_57 (
    .in0({multiplexer_50_out, multiplexer_49_out}), .in1({multiplexer_52_out, multiplexer_51_out}),
    .out(multiplexer_57_out), .sel(B[3]));  // open: en
  Multiplexer #(.width(8)) multiplexer_58 (
    .in0({multiplexer_52_out, multiplexer_51_out}), .in1({multiplexer_54_out, multiplexer_53_out}),
    .out(multiplexer_58_out), .sel(B[3]));  // open: en
  Multiplexer #(.width(8)) multiplexer_59 (
    .in0({multiplexer_54_out, multiplexer_53_out}), .in1({multiplexer_56_out, multiplexer_55_out}),
    .out(multiplexer_59_out), .sel(B[3]));  // open: en
  Multiplexer #(.width(8)) multiplexer_60 (
    .in0({multiplexer_56_out, multiplexer_55_out}), .in1({8{1'b0}}), .out(multiplexer_60_out), .sel(B[3]));  // open: en
  Multiplexer #(.width(16)) multiplexer_61 (
    .in0({multiplexer_58_out, multiplexer_57_out}), .in1({multiplexer_60_out, multiplexer_59_out}),
    .out(Result[15:0]), .sel(B[4]));  // open: en
  Multiplexer #(.width(16)) multiplexer_62 (
    .in0({multiplexer_60_out, multiplexer_59_out}), .in1({16{1'b0}}), .out(Result[31:16]), .sel(B[4]));  // open: en

  // Other names for the same wires on the sheet: b_0 = B[0]; b_1 = B[1]; b_2 = B[2]; b_3 = B[3]; b_4 = B[4]
endmodule

module shift_arithmetic_right (
  input  [31:0] A,
  input  [31:0] B,
  output [31:0] Result
);

  wire [1:0] bit_extender_1_out, multiplexer_1_out, multiplexer_3_out, multiplexer_5_out, multiplexer_7_out,
       multiplexer_9_out, multiplexer_11_out, multiplexer_13_out, multiplexer_15_out, multiplexer_17_out,
       multiplexer_19_out, multiplexer_21_out, multiplexer_23_out, multiplexer_25_out, multiplexer_27_out,
       multiplexer_29_out, multiplexer_31_out, multiplexer_33_out, multiplexer_34_out, multiplexer_35_out,
       multiplexer_36_out, multiplexer_37_out, multiplexer_38_out, multiplexer_39_out, multiplexer_40_out,
       multiplexer_41_out, multiplexer_42_out, multiplexer_43_out, multiplexer_44_out, multiplexer_45_out,
       multiplexer_46_out, multiplexer_47_out, multiplexer_48_out;
  wire [3:0] bit_extender_2_out, multiplexer_49_out, multiplexer_50_out, multiplexer_51_out,
       multiplexer_52_out, multiplexer_53_out, multiplexer_54_out, multiplexer_55_out, multiplexer_56_out;
  wire [7:0] bit_extender_3_out, multiplexer_57_out, multiplexer_58_out, multiplexer_59_out,
       multiplexer_60_out;
  wire [15:0] bit_extender_4_out;

  Multiplexer multiplexer_1 (.in0(A[0]), .in1(A[1]), .out(multiplexer_1_out[0]), .sel(B[0]));  // open: en
  Multiplexer multiplexer_2 (.in0(A[1]), .in1(A[2]), .out(multiplexer_1_out[1]), .sel(B[0]));  // open: en
  Multiplexer multiplexer_3 (.in0(A[2]), .in1(A[3]), .out(multiplexer_3_out[0]), .sel(B[0]));  // open: en
  Multiplexer multiplexer_4 (.in0(A[3]), .in1(A[4]), .out(multiplexer_3_out[1]), .sel(B[0]));  // open: en
  Multiplexer multiplexer_5 (.in0(A[4]), .in1(A[5]), .out(multiplexer_5_out[0]), .sel(B[0]));  // open: en
  Multiplexer multiplexer_6 (.in0(A[5]), .in1(A[6]), .out(multiplexer_5_out[1]), .sel(B[0]));  // open: en
  Multiplexer multiplexer_7 (.in0(A[6]), .in1(A[7]), .out(multiplexer_7_out[0]), .sel(B[0]));  // open: en
  Multiplexer multiplexer_8 (.in0(A[7]), .in1(A[8]), .out(multiplexer_7_out[1]), .sel(B[0]));  // open: en
  Multiplexer multiplexer_9 (.in0(A[8]), .in1(A[9]), .out(multiplexer_9_out[0]), .sel(B[0]));  // open: en
  Multiplexer multiplexer_10 (.in0(A[9]), .in1(A[10]), .out(multiplexer_9_out[1]), .sel(B[0]));  // open: en
  Multiplexer multiplexer_11 (.in0(A[10]), .in1(A[11]), .out(multiplexer_11_out[0]), .sel(B[0]));  // open: en
  Multiplexer multiplexer_12 (.in0(A[11]), .in1(A[12]), .out(multiplexer_11_out[1]), .sel(B[0]));  // open: en
  Multiplexer multiplexer_13 (.in0(A[12]), .in1(A[13]), .out(multiplexer_13_out[0]), .sel(B[0]));  // open: en
  Multiplexer multiplexer_14 (.in0(A[13]), .in1(A[14]), .out(multiplexer_13_out[1]), .sel(B[0]));  // open: en
  Multiplexer multiplexer_15 (.in0(A[14]), .in1(A[15]), .out(multiplexer_15_out[0]), .sel(B[0]));  // open: en
  Multiplexer multiplexer_16 (.in0(A[15]), .in1(A[16]), .out(multiplexer_15_out[1]), .sel(B[0]));  // open: en
  Multiplexer multiplexer_17 (.in0(A[16]), .in1(A[17]), .out(multiplexer_17_out[0]), .sel(B[0]));  // open: en
  Multiplexer multiplexer_18 (.in0(A[17]), .in1(A[18]), .out(multiplexer_17_out[1]), .sel(B[0]));  // open: en
  Multiplexer multiplexer_19 (.in0(A[18]), .in1(A[19]), .out(multiplexer_19_out[0]), .sel(B[0]));  // open: en
  Multiplexer multiplexer_20 (.in0(A[19]), .in1(A[20]), .out(multiplexer_19_out[1]), .sel(B[0]));  // open: en
  Multiplexer multiplexer_21 (.in0(A[20]), .in1(A[21]), .out(multiplexer_21_out[0]), .sel(B[0]));  // open: en
  Multiplexer multiplexer_22 (.in0(A[21]), .in1(A[22]), .out(multiplexer_21_out[1]), .sel(B[0]));  // open: en
  Multiplexer multiplexer_23 (.in0(A[22]), .in1(A[23]), .out(multiplexer_23_out[0]), .sel(B[0]));  // open: en
  Multiplexer multiplexer_24 (.in0(A[23]), .in1(A[24]), .out(multiplexer_23_out[1]), .sel(B[0]));  // open: en
  Multiplexer multiplexer_25 (.in0(A[24]), .in1(A[25]), .out(multiplexer_25_out[0]), .sel(B[0]));  // open: en
  Multiplexer multiplexer_26 (.in0(A[25]), .in1(A[26]), .out(multiplexer_25_out[1]), .sel(B[0]));  // open: en
  Multiplexer multiplexer_27 (.in0(A[26]), .in1(A[27]), .out(multiplexer_27_out[0]), .sel(B[0]));  // open: en
  Multiplexer multiplexer_28 (.in0(A[27]), .in1(A[28]), .out(multiplexer_27_out[1]), .sel(B[0]));  // open: en
  Multiplexer multiplexer_29 (.in0(A[28]), .in1(A[29]), .out(multiplexer_29_out[0]), .sel(B[0]));  // open: en
  Multiplexer multiplexer_30 (.in0(A[29]), .in1(A[30]), .out(multiplexer_29_out[1]), .sel(B[0]));  // open: en
  Multiplexer multiplexer_31 (.in0(A[30]), .in1(A[31]), .out(multiplexer_31_out[0]), .sel(B[0]));  // open: en
  Multiplexer multiplexer_32 (.in0(A[31]), .in1(A[31]), .out(multiplexer_31_out[1]), .sel(B[0]));  // open: en
  assign bit_extender_1_out = {{1{A[31]}}, A[31]};  // Bit_Extender bit_extender_1
  Multiplexer #(.width(2)) multiplexer_33 (
    .in0(multiplexer_1_out), .in1(multiplexer_3_out), .out(multiplexer_33_out), .sel(B[1]));  // open: en
  Multiplexer #(.width(2)) multiplexer_34 (
    .in0(multiplexer_3_out), .in1(multiplexer_5_out), .out(multiplexer_34_out), .sel(B[1]));  // open: en
  Multiplexer #(.width(2)) multiplexer_35 (
    .in0(multiplexer_5_out), .in1(multiplexer_7_out), .out(multiplexer_35_out), .sel(B[1]));  // open: en
  Multiplexer #(.width(2)) multiplexer_36 (
    .in0(multiplexer_7_out), .in1(multiplexer_9_out), .out(multiplexer_36_out), .sel(B[1]));  // open: en
  Multiplexer #(.width(2)) multiplexer_37 (
    .in0(multiplexer_9_out), .in1(multiplexer_11_out), .out(multiplexer_37_out), .sel(B[1]));  // open: en
  Multiplexer #(.width(2)) multiplexer_38 (
    .in0(multiplexer_11_out), .in1(multiplexer_13_out), .out(multiplexer_38_out), .sel(B[1]));  // open: en
  Multiplexer #(.width(2)) multiplexer_39 (
    .in0(multiplexer_13_out), .in1(multiplexer_15_out), .out(multiplexer_39_out), .sel(B[1]));  // open: en
  Multiplexer #(.width(2)) multiplexer_40 (
    .in0(multiplexer_15_out), .in1(multiplexer_17_out), .out(multiplexer_40_out), .sel(B[1]));  // open: en
  Multiplexer #(.width(2)) multiplexer_41 (
    .in0(multiplexer_17_out), .in1(multiplexer_19_out), .out(multiplexer_41_out), .sel(B[1]));  // open: en
  Multiplexer #(.width(2)) multiplexer_42 (
    .in0(multiplexer_19_out), .in1(multiplexer_21_out), .out(multiplexer_42_out), .sel(B[1]));  // open: en
  Multiplexer #(.width(2)) multiplexer_43 (
    .in0(multiplexer_21_out), .in1(multiplexer_23_out), .out(multiplexer_43_out), .sel(B[1]));  // open: en
  Multiplexer #(.width(2)) multiplexer_44 (
    .in0(multiplexer_23_out), .in1(multiplexer_25_out), .out(multiplexer_44_out), .sel(B[1]));  // open: en
  Multiplexer #(.width(2)) multiplexer_45 (
    .in0(multiplexer_25_out), .in1(multiplexer_27_out), .out(multiplexer_45_out), .sel(B[1]));  // open: en
  Multiplexer #(.width(2)) multiplexer_46 (
    .in0(multiplexer_27_out), .in1(multiplexer_29_out), .out(multiplexer_46_out), .sel(B[1]));  // open: en
  Multiplexer #(.width(2)) multiplexer_47 (
    .in0(multiplexer_29_out), .in1(multiplexer_31_out), .out(multiplexer_47_out), .sel(B[1]));  // open: en
  Multiplexer #(.width(2)) multiplexer_48 (
    .in0(multiplexer_31_out), .in1(bit_extender_1_out), .out(multiplexer_48_out), .sel(B[1]));  // open: en
  assign bit_extender_2_out = {{3{A[31]}}, A[31]};  // Bit_Extender bit_extender_2
  Multiplexer #(.width(4)) multiplexer_49 (
    .in0({multiplexer_34_out, multiplexer_33_out}), .in1({multiplexer_36_out, multiplexer_35_out}),
    .out(multiplexer_49_out), .sel(B[2]));  // open: en
  Multiplexer #(.width(4)) multiplexer_50 (
    .in0({multiplexer_36_out, multiplexer_35_out}), .in1({multiplexer_38_out, multiplexer_37_out}),
    .out(multiplexer_50_out), .sel(B[2]));  // open: en
  Multiplexer #(.width(4)) multiplexer_51 (
    .in0({multiplexer_38_out, multiplexer_37_out}), .in1({multiplexer_40_out, multiplexer_39_out}),
    .out(multiplexer_51_out), .sel(B[2]));  // open: en
  Multiplexer #(.width(4)) multiplexer_52 (
    .in0({multiplexer_40_out, multiplexer_39_out}), .in1({multiplexer_42_out, multiplexer_41_out}),
    .out(multiplexer_52_out), .sel(B[2]));  // open: en
  Multiplexer #(.width(4)) multiplexer_53 (
    .in0({multiplexer_42_out, multiplexer_41_out}), .in1({multiplexer_44_out, multiplexer_43_out}),
    .out(multiplexer_53_out), .sel(B[2]));  // open: en
  Multiplexer #(.width(4)) multiplexer_54 (
    .in0({multiplexer_44_out, multiplexer_43_out}), .in1({multiplexer_46_out, multiplexer_45_out}),
    .out(multiplexer_54_out), .sel(B[2]));  // open: en
  Multiplexer #(.width(4)) multiplexer_55 (
    .in0({multiplexer_46_out, multiplexer_45_out}), .in1({multiplexer_48_out, multiplexer_47_out}),
    .out(multiplexer_55_out), .sel(B[2]));  // open: en
  Multiplexer #(.width(4)) multiplexer_56 (
    .in0({multiplexer_48_out, multiplexer_47_out}), .in1(bit_extender_2_out), .out(multiplexer_56_out),
    .sel(B[2]));  // open: en
  assign bit_extender_3_out = {{7{A[31]}}, A[31]};  // Bit_Extender bit_extender_3
  Multiplexer #(.width(8)) multiplexer_57 (
    .in0({multiplexer_50_out, multiplexer_49_out}), .in1({multiplexer_52_out, multiplexer_51_out}),
    .out(multiplexer_57_out), .sel(B[3]));  // open: en
  Multiplexer #(.width(8)) multiplexer_58 (
    .in0({multiplexer_52_out, multiplexer_51_out}), .in1({multiplexer_54_out, multiplexer_53_out}),
    .out(multiplexer_58_out), .sel(B[3]));  // open: en
  Multiplexer #(.width(8)) multiplexer_59 (
    .in0({multiplexer_54_out, multiplexer_53_out}), .in1({multiplexer_56_out, multiplexer_55_out}),
    .out(multiplexer_59_out), .sel(B[3]));  // open: en
  Multiplexer #(.width(8)) multiplexer_60 (
    .in0({multiplexer_56_out, multiplexer_55_out}), .in1(bit_extender_3_out), .out(multiplexer_60_out),
    .sel(B[3]));  // open: en
  assign bit_extender_4_out = {{15{A[31]}}, A[31]};  // Bit_Extender bit_extender_4
  Multiplexer #(.width(16)) multiplexer_61 (
    .in0({multiplexer_58_out, multiplexer_57_out}), .in1({multiplexer_60_out, multiplexer_59_out}),
    .out(Result[15:0]), .sel(B[4]));  // open: en
  Multiplexer #(.width(16)) multiplexer_62 (
    .in0({multiplexer_60_out, multiplexer_59_out}), .in1(bit_extender_4_out), .out(Result[31:16]), .sel(B[4]));  // open: en

  // Other names for the same wires on the sheet: A_31 = A[31]; b_0 = B[0]; b_1 = B[1]; b_2 = B[2]; b_3 = B[3];
  //   b_4 = B[4]
endmodule

module mult (
  input  [31:0] A,
  input  [31:0] B,
  output [31:0] Result,
  output carry_out,
  output overflow
);

  wire mul_helper_1_carryout, mul_helper_1_overflow, mul_helper_2_carryout, mul_helper_2_overflow,
       mul_helper_3_carryout, mul_helper_3_overflow, mul_helper_4_carryout, mul_helper_4_overflow,
       mul_helper_5_carryout, mul_helper_5_overflow, mul_helper_6_carryout, mul_helper_6_overflow,
       mul_helper_7_carryout, mul_helper_7_overflow, mul_helper_8_carryout, mul_helper_8_overflow,
       mul_helper_9_carryout, mul_helper_9_overflow, mul_helper_10_carryout, mul_helper_10_overflow,
       mul_helper_11_carryout, mul_helper_11_overflow, mul_helper_12_carryout, mul_helper_12_overflow,
       mul_helper_13_carryout, mul_helper_13_overflow, mul_helper_14_carryout, mul_helper_14_overflow,
       mul_helper_15_carryout, mul_helper_15_overflow, mul_helper_16_carryout, mul_helper_16_overflow,
       mul_helper_17_carryout, mul_helper_17_overflow, mul_helper_18_carryout, mul_helper_18_overflow,
       mul_helper_19_carryout, mul_helper_19_overflow, mul_helper_20_carryout, mul_helper_20_overflow,
       mul_helper_21_carryout, mul_helper_21_overflow, mul_helper_22_carryout, mul_helper_22_overflow,
       mul_helper_23_carryout, mul_helper_23_overflow, mul_helper_24_carryout, mul_helper_24_overflow,
       mul_helper_25_carryout, mul_helper_25_overflow, mul_helper_26_carryout, mul_helper_26_overflow,
       mul_helper_27_carryout, mul_helper_27_overflow, mul_helper_28_carryout, mul_helper_28_overflow,
       mul_helper_29_carryout, mul_helper_29_overflow, mul_helper_30_carryout, mul_helper_30_overflow,
       mul_helper_31_carryout, mul_helper_31_overflow, mul_helper_32_carryout, mul_helper_32_overflow;
  wire [31:0] mul_helper_1_product, mul_helper_1_shifted_a, mul_helper_2_product, mul_helper_2_shifted_a,
       mul_helper_3_product, mul_helper_3_shifted_a, mul_helper_4_product, mul_helper_4_shifted_a,
       mul_helper_5_product, mul_helper_5_shifted_a, mul_helper_6_product, mul_helper_6_shifted_a,
       mul_helper_7_product, mul_helper_7_shifted_a, mul_helper_8_product, mul_helper_8_shifted_a,
       mul_helper_9_product, mul_helper_9_shifted_a, mul_helper_10_product, mul_helper_10_shifted_a,
       mul_helper_11_product, mul_helper_11_shifted_a, mul_helper_12_product, mul_helper_12_shifted_a,
       mul_helper_13_product, mul_helper_13_shifted_a, mul_helper_14_product, mul_helper_14_shifted_a,
       mul_helper_15_product, mul_helper_15_shifted_a, mul_helper_16_product, mul_helper_16_shifted_a,
       mul_helper_17_product, mul_helper_17_shifted_a, mul_helper_18_product, mul_helper_18_shifted_a,
       mul_helper_19_product, mul_helper_19_shifted_a, mul_helper_20_product, mul_helper_20_shifted_a,
       mul_helper_21_product, mul_helper_21_shifted_a, mul_helper_22_product, mul_helper_22_shifted_a,
       mul_helper_23_product, mul_helper_23_shifted_a, mul_helper_24_product, mul_helper_24_shifted_a,
       mul_helper_25_product, mul_helper_25_shifted_a, mul_helper_26_product, mul_helper_26_shifted_a,
       mul_helper_27_product, mul_helper_27_shifted_a, mul_helper_28_product, mul_helper_28_shifted_a,
       mul_helper_29_product, mul_helper_29_shifted_a, mul_helper_30_product, mul_helper_30_shifted_a,
       mul_helper_31_product, mul_helper_31_shifted_a;

  mul_helper mul_helper_1 (
    .B_x(B[0]), .in_A(A), .current_product({32{1'b0}}), .shifted_a(mul_helper_1_shifted_a),
    .product(mul_helper_1_product), .overflow(mul_helper_1_overflow), .carryout(mul_helper_1_carryout));
  mul_helper mul_helper_2 (
    .B_x(B[1]), .in_A(mul_helper_1_shifted_a), .current_product(mul_helper_1_product),
    .shifted_a(mul_helper_2_shifted_a), .product(mul_helper_2_product), .overflow(mul_helper_2_overflow),
    .carryout(mul_helper_2_carryout));
  mul_helper mul_helper_3 (
    .B_x(B[2]), .in_A(mul_helper_2_shifted_a), .current_product(mul_helper_2_product),
    .shifted_a(mul_helper_3_shifted_a), .product(mul_helper_3_product), .overflow(mul_helper_3_overflow),
    .carryout(mul_helper_3_carryout));
  mul_helper mul_helper_4 (
    .B_x(B[3]), .in_A(mul_helper_3_shifted_a), .current_product(mul_helper_3_product),
    .shifted_a(mul_helper_4_shifted_a), .product(mul_helper_4_product), .overflow(mul_helper_4_overflow),
    .carryout(mul_helper_4_carryout));
  mul_helper mul_helper_5 (
    .B_x(B[4]), .in_A(mul_helper_4_shifted_a), .current_product(mul_helper_4_product),
    .shifted_a(mul_helper_5_shifted_a), .product(mul_helper_5_product), .overflow(mul_helper_5_overflow),
    .carryout(mul_helper_5_carryout));
  mul_helper mul_helper_6 (
    .B_x(B[5]), .in_A(mul_helper_5_shifted_a), .current_product(mul_helper_5_product),
    .shifted_a(mul_helper_6_shifted_a), .product(mul_helper_6_product), .overflow(mul_helper_6_overflow),
    .carryout(mul_helper_6_carryout));
  mul_helper mul_helper_7 (
    .B_x(B[6]), .in_A(mul_helper_6_shifted_a), .current_product(mul_helper_6_product),
    .shifted_a(mul_helper_7_shifted_a), .product(mul_helper_7_product), .overflow(mul_helper_7_overflow),
    .carryout(mul_helper_7_carryout));
  mul_helper mul_helper_8 (
    .B_x(B[7]), .in_A(mul_helper_7_shifted_a), .current_product(mul_helper_7_product),
    .shifted_a(mul_helper_8_shifted_a), .product(mul_helper_8_product), .overflow(mul_helper_8_overflow),
    .carryout(mul_helper_8_carryout));
  mul_helper mul_helper_9 (
    .B_x(B[8]), .in_A(mul_helper_8_shifted_a), .current_product(mul_helper_8_product),
    .shifted_a(mul_helper_9_shifted_a), .product(mul_helper_9_product), .overflow(mul_helper_9_overflow),
    .carryout(mul_helper_9_carryout));
  mul_helper mul_helper_10 (
    .B_x(B[9]), .in_A(mul_helper_9_shifted_a), .current_product(mul_helper_9_product),
    .shifted_a(mul_helper_10_shifted_a), .product(mul_helper_10_product), .overflow(mul_helper_10_overflow),
    .carryout(mul_helper_10_carryout));
  mul_helper mul_helper_11 (
    .B_x(B[10]), .in_A(mul_helper_10_shifted_a), .current_product(mul_helper_10_product),
    .shifted_a(mul_helper_11_shifted_a), .product(mul_helper_11_product), .overflow(mul_helper_11_overflow),
    .carryout(mul_helper_11_carryout));
  mul_helper mul_helper_12 (
    .B_x(B[11]), .in_A(mul_helper_11_shifted_a), .current_product(mul_helper_11_product),
    .shifted_a(mul_helper_12_shifted_a), .product(mul_helper_12_product), .overflow(mul_helper_12_overflow),
    .carryout(mul_helper_12_carryout));
  mul_helper mul_helper_13 (
    .B_x(B[12]), .in_A(mul_helper_12_shifted_a), .current_product(mul_helper_12_product),
    .shifted_a(mul_helper_13_shifted_a), .product(mul_helper_13_product), .overflow(mul_helper_13_overflow),
    .carryout(mul_helper_13_carryout));
  mul_helper mul_helper_14 (
    .B_x(B[13]), .in_A(mul_helper_13_shifted_a), .current_product(mul_helper_13_product),
    .shifted_a(mul_helper_14_shifted_a), .product(mul_helper_14_product), .overflow(mul_helper_14_overflow),
    .carryout(mul_helper_14_carryout));
  mul_helper mul_helper_15 (
    .B_x(B[14]), .in_A(mul_helper_14_shifted_a), .current_product(mul_helper_14_product),
    .shifted_a(mul_helper_15_shifted_a), .product(mul_helper_15_product), .overflow(mul_helper_15_overflow),
    .carryout(mul_helper_15_carryout));
  mul_helper mul_helper_16 (
    .B_x(B[15]), .in_A(mul_helper_15_shifted_a), .current_product(mul_helper_15_product),
    .shifted_a(mul_helper_16_shifted_a), .product(mul_helper_16_product), .overflow(mul_helper_16_overflow),
    .carryout(mul_helper_16_carryout));
  mul_helper mul_helper_17 (
    .B_x(B[16]), .in_A(mul_helper_16_shifted_a), .current_product(mul_helper_16_product),
    .shifted_a(mul_helper_17_shifted_a), .product(mul_helper_17_product), .overflow(mul_helper_17_overflow),
    .carryout(mul_helper_17_carryout));
  mul_helper mul_helper_18 (
    .B_x(B[17]), .in_A(mul_helper_17_shifted_a), .current_product(mul_helper_17_product),
    .shifted_a(mul_helper_18_shifted_a), .product(mul_helper_18_product), .overflow(mul_helper_18_overflow),
    .carryout(mul_helper_18_carryout));
  mul_helper mul_helper_19 (
    .B_x(B[18]), .in_A(mul_helper_18_shifted_a), .current_product(mul_helper_18_product),
    .shifted_a(mul_helper_19_shifted_a), .product(mul_helper_19_product), .overflow(mul_helper_19_overflow),
    .carryout(mul_helper_19_carryout));
  mul_helper mul_helper_20 (
    .B_x(B[19]), .in_A(mul_helper_19_shifted_a), .current_product(mul_helper_19_product),
    .shifted_a(mul_helper_20_shifted_a), .product(mul_helper_20_product), .overflow(mul_helper_20_overflow),
    .carryout(mul_helper_20_carryout));
  mul_helper mul_helper_21 (
    .B_x(B[20]), .in_A(mul_helper_20_shifted_a), .current_product(mul_helper_20_product),
    .shifted_a(mul_helper_21_shifted_a), .product(mul_helper_21_product), .overflow(mul_helper_21_overflow),
    .carryout(mul_helper_21_carryout));
  mul_helper mul_helper_22 (
    .B_x(B[21]), .in_A(mul_helper_21_shifted_a), .current_product(mul_helper_21_product),
    .shifted_a(mul_helper_22_shifted_a), .product(mul_helper_22_product), .overflow(mul_helper_22_overflow),
    .carryout(mul_helper_22_carryout));
  mul_helper mul_helper_23 (
    .B_x(B[22]), .in_A(mul_helper_22_shifted_a), .current_product(mul_helper_22_product),
    .shifted_a(mul_helper_23_shifted_a), .product(mul_helper_23_product), .overflow(mul_helper_23_overflow),
    .carryout(mul_helper_23_carryout));
  mul_helper mul_helper_24 (
    .B_x(B[23]), .in_A(mul_helper_23_shifted_a), .current_product(mul_helper_23_product),
    .shifted_a(mul_helper_24_shifted_a), .product(mul_helper_24_product), .overflow(mul_helper_24_overflow),
    .carryout(mul_helper_24_carryout));
  mul_helper mul_helper_25 (
    .B_x(B[24]), .in_A(mul_helper_24_shifted_a), .current_product(mul_helper_24_product),
    .shifted_a(mul_helper_25_shifted_a), .product(mul_helper_25_product), .overflow(mul_helper_25_overflow),
    .carryout(mul_helper_25_carryout));
  mul_helper mul_helper_26 (
    .B_x(B[25]), .in_A(mul_helper_25_shifted_a), .current_product(mul_helper_25_product),
    .shifted_a(mul_helper_26_shifted_a), .product(mul_helper_26_product), .overflow(mul_helper_26_overflow),
    .carryout(mul_helper_26_carryout));
  mul_helper mul_helper_27 (
    .B_x(B[26]), .in_A(mul_helper_26_shifted_a), .current_product(mul_helper_26_product),
    .shifted_a(mul_helper_27_shifted_a), .product(mul_helper_27_product), .overflow(mul_helper_27_overflow),
    .carryout(mul_helper_27_carryout));
  mul_helper mul_helper_28 (
    .B_x(B[27]), .in_A(mul_helper_27_shifted_a), .current_product(mul_helper_27_product),
    .shifted_a(mul_helper_28_shifted_a), .product(mul_helper_28_product), .overflow(mul_helper_28_overflow),
    .carryout(mul_helper_28_carryout));
  mul_helper mul_helper_29 (
    .B_x(B[28]), .in_A(mul_helper_28_shifted_a), .current_product(mul_helper_28_product),
    .shifted_a(mul_helper_29_shifted_a), .product(mul_helper_29_product), .overflow(mul_helper_29_overflow),
    .carryout(mul_helper_29_carryout));
  mul_helper mul_helper_30 (
    .B_x(B[29]), .in_A(mul_helper_29_shifted_a), .current_product(mul_helper_29_product),
    .shifted_a(mul_helper_30_shifted_a), .product(mul_helper_30_product), .overflow(mul_helper_30_overflow),
    .carryout(mul_helper_30_carryout));
  mul_helper mul_helper_31 (
    .B_x(B[30]), .in_A(mul_helper_30_shifted_a), .current_product(mul_helper_30_product),
    .shifted_a(mul_helper_31_shifted_a), .product(mul_helper_31_product), .overflow(mul_helper_31_overflow),
    .carryout(mul_helper_31_carryout));
  mul_helper mul_helper_32 (
    .B_x(B[31]), .in_A(mul_helper_31_shifted_a), .current_product(mul_helper_31_product), .product(Result),
    .overflow(mul_helper_32_overflow), .carryout(mul_helper_32_carryout));  // open: shifted_a
  or or_1 (carry_out, mul_helper_32_carryout, mul_helper_31_carryout, mul_helper_30_carryout, mul_helper_29_carryout, mul_helper_28_carryout, mul_helper_27_carryout, mul_helper_26_carryout, mul_helper_25_carryout, mul_helper_24_carryout, mul_helper_23_carryout, mul_helper_22_carryout, mul_helper_21_carryout, mul_helper_20_carryout, mul_helper_19_carryout, mul_helper_18_carryout, mul_helper_17_carryout, mul_helper_16_carryout, mul_helper_15_carryout, mul_helper_14_carryout, mul_helper_13_carryout, mul_helper_12_carryout, mul_helper_11_carryout, mul_helper_10_carryout, mul_helper_9_carryout, mul_helper_8_carryout, mul_helper_7_carryout, mul_helper_6_carryout, mul_helper_5_carryout, mul_helper_4_carryout, mul_helper_3_carryout, mul_helper_2_carryout, mul_helper_1_carryout);
  or or_2 (overflow, mul_helper_32_overflow, mul_helper_31_overflow, mul_helper_30_overflow, mul_helper_29_overflow, mul_helper_28_overflow, mul_helper_27_overflow, mul_helper_26_overflow, mul_helper_25_overflow, mul_helper_24_overflow, mul_helper_23_overflow, mul_helper_22_overflow, mul_helper_21_overflow, mul_helper_20_overflow, mul_helper_19_overflow, mul_helper_18_overflow, mul_helper_17_overflow, mul_helper_16_overflow, mul_helper_15_overflow, mul_helper_14_overflow, mul_helper_13_overflow, mul_helper_12_overflow, mul_helper_11_overflow, mul_helper_10_overflow, mul_helper_9_overflow, mul_helper_8_overflow, mul_helper_7_overflow, mul_helper_6_overflow, mul_helper_5_overflow, mul_helper_4_overflow, mul_helper_3_overflow, mul_helper_2_overflow, mul_helper_1_overflow);

  // Other names for the same wires on the sheet: b_0 = B[0]; b_1 = B[1]; b_2 = B[2]; b_3 = B[3]; b_4 = B[4];
  //   b_5 = B[5]; b_6 = B[6]; b_7 = B[7]; b_8 = B[8]; b_9 = B[9]; b_10 = B[10]; b_11 = B[11]; b_12 = B[12];
  //   b_13 = B[13]; b_14 = B[14]; b_15 = B[15]; b_16 = B[16]; b_17 = B[17]; b_18 = B[18]; b_19 = B[19]; b_20 = B[20];
  //   b_21 = B[21]; b_22 = B[22]; b_23 = B[23]; b_24 = B[24]; b_25 = B[25]; b_26 = B[26]; b_27 = B[27]; b_28 = B[28];
  //   b_29 = B[29]; b_30 = B[30]; b_31 = B[31]
endmodule

module equal (
  input  [31:0] A,
  input  [31:0] B,
  output Result
);

  wire or_1_out;
  wire [31:0] n32_bit_subs_1_result;

  _32_bit_subs u_32_bit_subs_1 (.A(A), .B(B), .Result(n32_bit_subs_1_result));  // open: carry_out, overflow
  or or_1 (or_1_out, n32_bit_subs_1_result[0], n32_bit_subs_1_result[1], n32_bit_subs_1_result[2], n32_bit_subs_1_result[3], n32_bit_subs_1_result[4], n32_bit_subs_1_result[5], n32_bit_subs_1_result[6], n32_bit_subs_1_result[7], n32_bit_subs_1_result[8], n32_bit_subs_1_result[9], n32_bit_subs_1_result[10], n32_bit_subs_1_result[11], n32_bit_subs_1_result[12], n32_bit_subs_1_result[13], n32_bit_subs_1_result[14], n32_bit_subs_1_result[15], n32_bit_subs_1_result[16], n32_bit_subs_1_result[17], n32_bit_subs_1_result[18], n32_bit_subs_1_result[19], n32_bit_subs_1_result[20], n32_bit_subs_1_result[21], n32_bit_subs_1_result[22], n32_bit_subs_1_result[23], n32_bit_subs_1_result[24], n32_bit_subs_1_result[25], n32_bit_subs_1_result[26], n32_bit_subs_1_result[27], n32_bit_subs_1_result[28], n32_bit_subs_1_result[29], n32_bit_subs_1_result[30], n32_bit_subs_1_result[31]);
  not not_1 (Result, or_1_out);
endmodule

module mul_helper (
  input  [31:0] in_A,
  input  [31:0] current_product,
  input  B_x,
  output overflow,
  output carryout,
  output [31:0] shifted_a,
  output [31:0] product
);

  wire n32_bit_adder_1_carry_out, n32_bit_adder_1_overflow;
  wire [31:0] n32_bit_adder_1_result;

  shift_left shift_left_1 (.A(in_A), .B(32'h1), .Result(shifted_a));
  _32_bit_adder u_32_bit_adder_1 (
    .A(current_product), .B(in_A), .carry_out(n32_bit_adder_1_carry_out),
    .overflow(n32_bit_adder_1_overflow), .Result(n32_bit_adder_1_result));
  Multiplexer #(.width(32)) multiplexer_1 (
    .in0(current_product), .in1(n32_bit_adder_1_result), .out(product), .sel(B_x));  // open: en
  Multiplexer multiplexer_2 (.in0(1'b0), .in1(n32_bit_adder_1_overflow), .out(overflow), .sel(B_x));  // open: en
  Multiplexer multiplexer_3 (.in0(1'b0), .in1(n32_bit_adder_1_carry_out), .out(carryout), .sel(B_x));  // open: en
endmodule

module SingleCycleProcessor (
  output overflow
);

  wire ALUControl_branch, and_1_out, Clock, Control_Unit_alusrc, Control_Unit_branch, Control_Unit_jump,
       Control_Unit_memread, Control_Unit_memtoreg, Control_Unit_memwrite, Control_Unit_regdes,
       Control_Unit_regwrite, RESET_2_out, RESET_3_out, RESET_out;
  wire [4:0] multiplexer_1_out;
  wire [5:0] ALUControl_out, Control_Unit_aluop;
  wire [15:0] bit_extender_1_out, bit_extender_4_out;
  wire [31:0] add_result, ALU_out_c, bit_extender_2_out, bit_extender_3_out, counter_1_q, multiplexer_2_out,
       multiplexer_3_out, multiplexer_4_out, ram_1_data, ram_2_data, registerfile_1_p1, registerfile_1_p7,
       registerfile_1_p8;

  Clock clock_1 (.out(Clock));
  Counter #(.width(32), .max('he), .ongoal("stay")) counter_1 (
    .load(1'b1), .D(multiplexer_4_out), .count(1'b0), .Q(counter_1_q), .clk(Clock), .clr(RESET_out));  // open: carry
  Button RESET (.out(RESET_out));
  Bit_Extender #(.in_width(32)) bit_extender_1 (.in(counter_1_q), .out(bit_extender_1_out));
  _32_bit_adder add (.A(counter_1_q), .B(32'h1), .Result(add_result));  // open: carry_out, overflow
  Button RESET_2 (.out(RESET_2_out));
  RAM #(.addrWidth(16), .dataWidth(32)) ram_1 (
    .addr(bit_extender_1_out), .data(ram_1_data), .sel(1'b1), .clk(Clock), .ld(1'b1), .clr(RESET_2_out));
  assign bit_extender_2_out = {{6{1'b0}}, ram_1_data[25:0]};  // Bit_Extender bit_extender_2
  control_unit Control_Unit (
    .Instr_31_26(ram_1_data[31:26]), .RegDes(Control_Unit_regdes), .Jump(Control_Unit_jump),
    .Branch(Control_Unit_branch), .MemRead(Control_Unit_memread), .MemToReg(Control_Unit_memtoreg),
    .MemWrite(Control_Unit_memwrite), .ALUSrc(Control_Unit_alusrc), .RegWrite(Control_Unit_regwrite),
    .ALUOp(Control_Unit_aluop));
  Multiplexer #(.width(5)) multiplexer_1 (
    .in0(ram_1_data[20:16]), .in1(ram_1_data[15:11]), .out(multiplexer_1_out), .sel(Control_Unit_regdes));  // open: en
  // RegisterFile registerfile_1: pin names not known; wires that end beside it: registerfile_1_p1, Clock, Control_Unit_regwrite, multiplexer_1_out, ram_1_data[25:21], ram_1_data[20:16], registerfile_1_p7, registerfile_1_p8
  assign bit_extender_3_out = {{16{ram_1_data[15]}}, ram_1_data[15:0]};  // Bit_Extender bit_extender_3
  Multiplexer #(.width(32)) multiplexer_2 (
    .in0(registerfile_1_p8), .in1(bit_extender_3_out), .out(multiplexer_2_out), .sel(Control_Unit_alusrc));  // open: en
  ALUControl ALUControl (
    .Function(ram_1_data[5:0]), .in_1(registerfile_1_p7), .in_2(multiplexer_2_out),
    .ALUOp(Control_Unit_aluop), .out(ALUControl_out), .Branch(ALUControl_branch));
  ALU ALU (
    .in_A(registerfile_1_p7), .in_B(multiplexer_2_out), .overflow(overflow), .opcode(ALUControl_out),
    .out_C(ALU_out_c));  // open: carryout, zero
  and and_1 (and_1_out, Control_Unit_branch, ALUControl_branch);
  Multiplexer #(.width(32)) multiplexer_3 (
    .in0(add_result), .in1(bit_extender_3_out), .out(multiplexer_3_out), .sel(and_1_out));  // open: en
  Bit_Extender #(.in_width(32)) bit_extender_4 (.in(ALU_out_c), .out(bit_extender_4_out));
  Multiplexer #(.width(32)) multiplexer_4 (
    .in0(multiplexer_3_out), .in1(bit_extender_2_out), .out(multiplexer_4_out), .sel(Control_Unit_jump));  // open: en
  RAM #(.addrWidth(16), .dataWidth(32), .bus("separate")) ram_2 (
    .addr(bit_extender_4_out), .din(registerfile_1_p8), .data(ram_2_data), .str(Control_Unit_memwrite),
    .sel(1'b1), .clk(Clock), .ld(Control_Unit_memread), .clr(RESET_3_out));
  Button RESET_3 (.out(RESET_3_out));
  Multiplexer #(.width(32)) multiplexer_5 (
    .in0(ALU_out_c), .in1(ram_2_data), .out(registerfile_1_p1), .sel(Control_Unit_memtoreg));  // open: en

  // Notes on the sheet:
  //   PC
  //   Instruction Memory
  //   Instr[25-0]
  //   RegDest
  //   Inst 25-21
  //   Inst 20-16
  //   Inst 15-11
  //   Write Data
  //   Inst 31-26
  //   RegWrite
  //   ALUSrc
  //   ALUOp
  //   Inst 15-0
  //   Inst 5-0
  //   Jump
  //   Branch
  //   MemWrite
  //   MemRead
  //   MemToReg
  //   Data Memory
endmodule

module control_unit (
  input  [5:0] Instr_31_26,
  output Jump,
  output Branch,
  output MemRead,
  output MemToReg,
  output MemWrite,
  output ALUSrc,
  output RegWrite,
  output [5:0] ALUOp,
  output RegDes
);

  wire [3:0] bit_extender_1_out;
  wire [7:0] undriven;

  Bit_Extender #(.in_width(6), .out_width(4)) bit_extender_1 (.in(Instr_31_26), .out(bit_extender_1_out));
  Multiplexer #(.select(4), .width(8)) multiplexer_1 (
    .in0(8'hc0), .in1(8'hc0), .in2(8'hc0), .in3(8'hc0), .in4(8'hc0), .in5(8'hc0), .in6(8'hc0), .in7(8'hc0),
    .in8(8'hc0), .in9(8'hc0), .in10(8'h6c), .in11(8'h78), .in12(8'h2), .in13(8'h2), .in14(8'h1),
    .in15(undriven), .out({RegDes, RegWrite, ALUSrc, MemWrite, MemToReg, MemRead, Branch, Jump}),
    .sel(bit_extender_1_out));  // open: en

  assign ALUOp = Instr_31_26;
endmodule

module ALUControl (
  input  [31:0] in_1,
  input  [31:0] in_2,
  input  [5:0] Function,
  input  [5:0] ALUOp,
  output [5:0] out,
  output Branch
);

  wire bit_extender_2_out, equal_1_result, not_1_out;
  wire [3:0] bit_extender_1_out;
  wire [5:0] undriven;
  wire [31:0] n32_bit_subs_1_result;

  _32_bit_subs u_32_bit_subs_1 (.A(in_1), .B(in_2), .Result(n32_bit_subs_1_result));  // open: carry_out, overflow
  Bit_Extender #(.in_width(6), .out_width(4)) bit_extender_1 (.in(ALUOp), .out(bit_extender_1_out));
  Bit_Extender #(.in_width(6), .out_width(1)) bit_extender_2 (.in(ALUOp), .out(bit_extender_2_out));
  equal equal_1 (.A(n32_bit_subs_1_result), .B({32{1'b0}}), .Result(equal_1_result));
  Multiplexer #(.select(4), .width(6)) multiplexer_1 (
    .in0(ALUOp), .in1(ALUOp), .in2(ALUOp), .in3(ALUOp), .in4(ALUOp), .in5(ALUOp), .in6(ALUOp), .in7(ALUOp),
    .in8(ALUOp), .in9(ALUOp), .in10(6'b000001), .in11(6'b000001), .in12({6{1'b0}}), .in13({6{1'b0}}),
    .in14({6{1'b0}}), .in15(undriven), .out(out), .sel(bit_extender_1_out));  // open: en
  not not_1 (not_1_out, equal_1_result);
  Multiplexer multiplexer_2 (
    .in0(equal_1_result), .in1(not_1_out), .out(Branch), .sel(bit_extender_2_out));  // open: en

  // Other names for the same wires on the sheet: A[31:0] = in_1; B[31:0] = in_2
endmodule
