// Logisim project two_bit_register.circ as structural Verilog: 1 circuit, main circuit main
module main (
  input  [1:0] A1,
  input  [1:0] A2,
  input  [31:0] WD,
  input  [1:0] A3,
  input  Write_EN,
  output [31:0] RD1,
  output [31:0] RD2
);

  wire clock_1_out, demultiplexer_2_out0, demultiplexer_2_out1, demultiplexer_2_out2, demultiplexer_2_out3;
  wire [31:0] Address00_q, Address01_q, Address10_q, Address11_q, demultiplexer_1_out0, demultiplexer_1_out1,
       demultiplexer_1_out2, demultiplexer_1_out3;

  Demultiplexer #(.select(2)) demultiplexer_1 (
    .out0(demultiplexer_1_out0[0]), .out1(demultiplexer_1_out1[0]), .out2(demultiplexer_1_out2[0]),
    .out3(demultiplexer_1_out3[0]), .in(WD[0]), .sel(A3));  // open: en
  Demultiplexer #(.select(2)) demultiplexer_2 (
    .out0(demultiplexer_2_out0), .out1(demultiplexer_2_out1), .out2(demultiplexer_2_out2),
    .out3(demultiplexer_2_out3), .in(Write_EN), .sel(A3));  // open: en
  Clock clock_1 (.out(clock_1_out));
  Register #(.width(32)) Address00 (
    .D(demultiplexer_1_out0), .en(demultiplexer_2_out0), .Q(Address00_q), .clk(clock_1_out));  // open: clr
  Register #(.width(32)) Address01 (
    .D(demultiplexer_1_out1), .en(demultiplexer_2_out1), .Q(Address01_q), .clk(clock_1_out));  // open: clr
  Register #(.width(32)) Address10 (
    .D(demultiplexer_1_out2), .en(demultiplexer_2_out2), .Q(Address10_q), .clk(clock_1_out));  // open: clr
  Register #(.width(32)) Address11 (
    .D(demultiplexer_1_out3), .en(demultiplexer_2_out3), .Q(Address11_q), .clk(clock_1_out));  // open: clr
  Multiplexer #(.select(2)) multiplexer_1 (
    .in0(Address00_q[0]), .in1(Address01_q[0]), .in2(Address10_q[0]), .in3(Address11_q[0]), .out(RD2[0]),
    .sel(A2));  // open: en
  Multiplexer #(.select(2)) multiplexer_2 (
    .in0(Address00_q[0]), .in1(Address01_q[0]), .in2(Address10_q[0]), .in3(Address11_q[0]), .out(RD1[0]),
    .sel(A1));  // open: en
  // Pins of 1 and 32 bits meet at RD1
  // Pins of 1 and 32 bits meet at RD2
  // Pins of 1 and 32 bits meet at demultiplexer_1_out2
  // Pins of 1 and 32 bits meet at Address10_q
  // Pins of 1 and 32 bits meet at Address00_q
  // Pins of 1 and 32 bits meet at Address01_q
  // Pins of 1 and 32 bits meet at Address11_q
  // Pins of 1 and 32 bits meet at demultiplexer_1_out0
  // Pins of 1 and 32 bits meet at demultiplexer_1_out1
  // Pins of 1 and 32 bits meet at demultiplexer_1_out3
  // Pins of 1 and 32 bits meet at WD
endmodule
